// Logisim project 8BIT_ALU.circ as structural Verilog: 33 circuits, main circuit 8BIT_ADDITION_SUBTRACTION_CIRCUIT
// ADD_SUB
module _8BIT_ADDITION_SUBTRACTION_CIRCUIT (
  input  ADD_SUB_SIGNAL,
  input  [7:0] A,
  input  [7:0] B,
  output [7:0] SUM_DIFF,
  output COUT_BOUT,
  output CIN_BIN_MSB
);

  wire [7:0] xor_1_out;

  xor xor_1 (xor_1_out[0], ADD_SUB_SIGNAL, B[0]);
  xor xor_2 (xor_1_out[1], ADD_SUB_SIGNAL, B[1]);
  xor xor_3 (xor_1_out[2], ADD_SUB_SIGNAL, B[2]);
  xor xor_4 (xor_1_out[3], ADD_SUB_SIGNAL, B[3]);
  xor xor_5 (xor_1_out[4], ADD_SUB_SIGNAL, B[4]);
  xor xor_6 (xor_1_out[5], ADD_SUB_SIGNAL, B[5]);
  xor xor_7 (xor_1_out[6], ADD_SUB_SIGNAL, B[6]);
  xor xor_8 (xor_1_out[7], ADD_SUB_SIGNAL, B[7]);
  _8BIT_PARALLEL_PREFIX_ADDER u_8bit_parallel_prefix_adder_1 (
    .A0_A7(A), .B0_B7(xor_1_out), .CIN(ADD_SUB_SIGNAL), .S0_S7(SUM_DIFF), .COUT(COUT_BOUT),
    .CIN_MSB(CIN_BIN_MSB));  // open: GG07, GP07
endmodule

// ADDER
module _8BIT_PARALLEL_PREFIX_ADDER (
  input  CIN,
  input  [7:0] A0_A7,
  input  [7:0] B0_B7,
  output [7:0] S0_S7,
  output COUT,
  output GG07,
  output GP07,
  output CIN_MSB
);

  wire n2bit_look_ahead_carry_unit_1_c2, n4bit_parallal_prefix_adder_1_gg03,
       n4bit_parallal_prefix_adder_1_gp03, n4bit_parallal_prefix_adder_2_gg03,
       n4bit_parallal_prefix_adder_2_gp03;

  _4BIT_PARALLAL_PREFIX_ADDER u_4bit_parallal_prefix_adder_1 (
    .A0_A3(A0_A7[3:0]), .B0_B3(B0_B7[3:0]), .CIN(CIN), .S0_S3(S0_S7[3:0]),
    .GG03(n4bit_parallal_prefix_adder_1_gg03), .GP03(n4bit_parallal_prefix_adder_1_gp03));  // open: COUT, CIN_MSB
  _4BIT_PARALLAL_PREFIX_ADDER u_4bit_parallal_prefix_adder_2 (
    .A0_A3(A0_A7[7:4]), .B0_B3(B0_B7[7:4]), .CIN(n2bit_look_ahead_carry_unit_1_c2), .S0_S3(S0_S7[7:4]),
    .GG03(n4bit_parallal_prefix_adder_2_gg03), .GP03(n4bit_parallal_prefix_adder_2_gp03), .CIN_MSB(CIN_MSB));  // open: COUT
  _2BIT_LOOK_AHEAD_CARRY_UNIT u_2bit_look_ahead_carry_unit_1 (
    .GG01(n4bit_parallal_prefix_adder_1_gg03), .GP01(n4bit_parallal_prefix_adder_1_gp03),
    .GG23(n4bit_parallal_prefix_adder_2_gg03), .GP23(n4bit_parallal_prefix_adder_2_gp03), .CIN(CIN),
    .C2(n2bit_look_ahead_carry_unit_1_c2), .C4(COUT), .GG03(GG07), .GP03(GP07));
endmodule

// ADDER
module _4BIT_PARALLAL_PREFIX_ADDER (
  input  CIN,
  input  [3:0] A0_A3,
  input  [3:0] B0_B3,
  output [3:0] S0_S3,
  output GG03,
  output GP03,
  output CIN_MSB,
  output COUT
);

  wire and_1_out, and_2_out, and_3_out, and_4_out, generate_propagate_1_gg, generate_propagate_1_gp,
       generate_propagate_2_gg, generate_propagate_2_gp, generate_propagate_3_gg, generate_propagate_3_gp,
       generate_propagate_4_gg, generate_propagate_4_gp, GG01_gg01, GG01_gp01, GG02_gg01, GG02_gp01,
       GG12_gg01, GG12_gp01, GG13_gg01, GG13_gp01, GG23_gg01, GG23_gp01, or_1_out, or_2_out;

  GENERATE_PROPAGATE generate_propagate_1 (
    .A(A0_A3[0]), .B(B0_B3[0]), .GG(generate_propagate_1_gg), .GP(generate_propagate_1_gp));
  GENERATE_PROPAGATE generate_propagate_2 (
    .A(A0_A3[1]), .B(B0_B3[1]), .GG(generate_propagate_2_gg), .GP(generate_propagate_2_gp));
  GENERATE_PROPAGATE generate_propagate_3 (
    .A(A0_A3[2]), .B(B0_B3[2]), .GG(generate_propagate_3_gg), .GP(generate_propagate_3_gp));
  GENERATE_PROPAGATE generate_propagate_4 (
    .A(A0_A3[3]), .B(B0_B3[3]), .GG(generate_propagate_4_gg), .GP(generate_propagate_4_gp));
  GROUP_GENERATE_PROPAGATE GG01 (
    .G0(generate_propagate_1_gg), .P0(generate_propagate_1_gp), .G1(generate_propagate_2_gg),
    .P1(generate_propagate_2_gp), .GG01(GG01_gg01), .GP01(GG01_gp01));
  GROUP_GENERATE_PROPAGATE GG12 (
    .G0(generate_propagate_2_gg), .P0(generate_propagate_2_gp), .G1(generate_propagate_3_gg),
    .P1(generate_propagate_3_gp), .GG01(GG12_gg01), .GP01(GG12_gp01));
  GROUP_GENERATE_PROPAGATE GG23 (
    .G0(generate_propagate_3_gg), .P0(generate_propagate_3_gp), .G1(generate_propagate_4_gg),
    .P1(generate_propagate_4_gp), .GG01(GG23_gg01), .GP01(GG23_gp01));
  GROUP_GENERATE_PROPAGATE GG02 (
    .G0(GG01_gg01), .P0(GG01_gp01), .G1(GG12_gg01), .P1(GG12_gp01), .GG01(GG02_gg01), .GP01(GG02_gp01));
  GROUP_GENERATE_PROPAGATE GG13 (
    .G0(GG12_gg01), .P0(GG12_gp01), .G1(GG23_gg01), .P1(GG23_gp01), .GG01(GG13_gg01), .GP01(GG13_gp01));
  GROUP_GENERATE_PROPAGATE u_GG03 (
    .G0(GG02_gg01), .P0(GG02_gp01), .G1(GG13_gg01), .P1(GG13_gp01), .GG01(GG03), .GP01(GP03));
  and and_1 (and_1_out, CIN, generate_propagate_1_gp);
  and and_2 (and_2_out, CIN, GG01_gp01);
  and and_3 (and_3_out, CIN, GG02_gp01);
  and and_4 (and_4_out, CIN, GP03);
  or or_1 (or_1_out, and_1_out, generate_propagate_1_gg);
  or or_2 (or_2_out, and_2_out, GG01_gg01);
  or or_3 (CIN_MSB, and_3_out, GG02_gg01);
  or or_4 (COUT, and_4_out, GG03);
  xor xor_1 (S0_S3[0], CIN, generate_propagate_1_gp);
  xor xor_2 (S0_S3[1], generate_propagate_2_gp, or_1_out);
  xor xor_3 (S0_S3[2], generate_propagate_3_gp, or_2_out);
  xor xor_4 (S0_S3[3], generate_propagate_4_gp, CIN_MSB);
endmodule

// 2BIT_LACU
module _2BIT_LOOK_AHEAD_CARRY_UNIT (
  input  CIN,
  input  GG01,
  input  GP01,
  input  GG23,
  input  GP23,
  output C2,
  output C4,
  output GG03,
  output GP03
);

  wire and_1_out, and_2_out;

  GROUP_GENERATE_PROPAGATE group_generate_propagate_1 (
    .G0(GG01), .P0(GP01), .G1(GG23), .P1(GP23), .GG01(GG03), .GP01(GP03));
  and and_1 (and_1_out, CIN, GP01);
  and and_2 (and_2_out, CIN, GP03);
  or or_1 (C2, and_1_out, GG01);
  or or_2 (C4, and_2_out, GG03);
endmodule

// MUX
module _8BIT_8_TO_1_MUX (
  input  S0,
  input  S1,
  input  S2,
  input  [7:0] DIN,
  input  [7:0] DIN_2,
  input  [7:0] DIN_3,
  input  [7:0] DIN_4,
  input  [7:0] DIN_5,
  input  [7:0] DIN_6,
  input  [7:0] DIN_7,
  input  [7:0] DIN_8,
  output [7:0] ALU_OUT
);

  wire [7:0] n8bit_2_to_1_mux_1_dout, n8bit_2_to_1_mux_2_dout, n8bit_2_to_1_mux_3_dout,
       n8bit_2_to_1_mux_4_dout, n8bit_2_to_1_mux_5_dout, n8bit_2_to_1_mux_6_dout;

  _8BIT_2_TO_1_MUX u_8bit_2_to_1_mux_1 (.DIN(DIN), .DIN_2(DIN_2), .SELECT(S0), .DOUT(n8bit_2_to_1_mux_1_dout));
  _8BIT_2_TO_1_MUX u_8bit_2_to_1_mux_2 (.DIN(DIN_3), .DIN_2(DIN_4), .SELECT(S0), .DOUT(n8bit_2_to_1_mux_2_dout));
  _8BIT_2_TO_1_MUX u_8bit_2_to_1_mux_3 (.DIN(DIN_5), .DIN_2(DIN_6), .SELECT(S0), .DOUT(n8bit_2_to_1_mux_3_dout));
  _8BIT_2_TO_1_MUX u_8bit_2_to_1_mux_4 (.DIN(DIN_7), .DIN_2(DIN_8), .SELECT(S0), .DOUT(n8bit_2_to_1_mux_4_dout));
  _8BIT_2_TO_1_MUX u_8bit_2_to_1_mux_5 (
    .DIN(n8bit_2_to_1_mux_1_dout), .DIN_2(n8bit_2_to_1_mux_2_dout), .SELECT(S1),
    .DOUT(n8bit_2_to_1_mux_5_dout));
  _8BIT_2_TO_1_MUX u_8bit_2_to_1_mux_6 (
    .DIN(n8bit_2_to_1_mux_3_dout), .DIN_2(n8bit_2_to_1_mux_4_dout), .SELECT(S1),
    .DOUT(n8bit_2_to_1_mux_6_dout));
  _8BIT_2_TO_1_MUX u_8bit_2_to_1_mux_7 (
    .DIN(n8bit_2_to_1_mux_5_dout), .DIN_2(n8bit_2_to_1_mux_6_dout), .SELECT(S2), .DOUT(ALU_OUT));
endmodule

// MUX
module _8BIT_4_TO_1_MUX (
  input  S0,
  input  S1,
  input  [7:0] DIN,
  input  [7:0] DIN_2,
  input  [7:0] DIN_3,
  input  [7:0] DIN_4,
  output [7:0] ALU_OUT
);

  wire [7:0] n8bit_2_to_1_mux_1_dout, n8bit_2_to_1_mux_2_dout;

  _8BIT_2_TO_1_MUX u_8bit_2_to_1_mux_1 (.DIN(DIN), .DIN_2(DIN_2), .SELECT(S0), .DOUT(n8bit_2_to_1_mux_1_dout));
  _8BIT_2_TO_1_MUX u_8bit_2_to_1_mux_2 (.DIN(DIN_3), .DIN_2(DIN_4), .SELECT(S0), .DOUT(n8bit_2_to_1_mux_2_dout));
  _8BIT_2_TO_1_MUX u_8bit_2_to_1_mux_3 (
    .DIN(n8bit_2_to_1_mux_1_dout), .DIN_2(n8bit_2_to_1_mux_2_dout), .SELECT(S1), .DOUT(ALU_OUT));
endmodule

// MUX
module _16BIT_2_TO_1_MUX (
  input  in_1,
  input  [15:0] DIN,
  input  [15:0] DIN_2,
  output [15:0] DOUT
);

  _8BIT_2_TO_1_MUX u_8bit_2_to_1_mux_1 (.DIN(DIN[7:0]), .DIN_2(DIN_2[7:0]), .SELECT(in_1), .DOUT(DOUT[7:0]));
  _8BIT_2_TO_1_MUX u_8bit_2_to_1_mux_2 (.DIN(DIN[15:8]), .DIN_2(DIN_2[15:8]), .SELECT(in_1), .DOUT(DOUT[15:8]));
endmodule

// MUX
module _8BIT_2_TO_1_MUX (
  input  SELECT,
  input  [7:0] DIN,
  input  [7:0] DIN_2,
  output [7:0] DOUT
);

  _1BIT_2_TO_1_MUX u_1bit_2_to_1_mux_1 (.DATA(DIN[0]), .DATA_2(DIN_2[0]), .SELECT(SELECT), .DOUT(DOUT[0]));
  _1BIT_2_TO_1_MUX u_1bit_2_to_1_mux_2 (.DATA(DIN[1]), .DATA_2(DIN_2[1]), .SELECT(SELECT), .DOUT(DOUT[1]));
  _1BIT_2_TO_1_MUX u_1bit_2_to_1_mux_3 (.DATA(DIN[2]), .DATA_2(DIN_2[2]), .SELECT(SELECT), .DOUT(DOUT[2]));
  _1BIT_2_TO_1_MUX u_1bit_2_to_1_mux_4 (.DATA(DIN[3]), .DATA_2(DIN_2[3]), .SELECT(SELECT), .DOUT(DOUT[3]));
  _1BIT_2_TO_1_MUX u_1bit_2_to_1_mux_5 (.DATA(DIN[4]), .DATA_2(DIN_2[4]), .SELECT(SELECT), .DOUT(DOUT[4]));
  _1BIT_2_TO_1_MUX u_1bit_2_to_1_mux_6 (.DATA(DIN[5]), .DATA_2(DIN_2[5]), .SELECT(SELECT), .DOUT(DOUT[5]));
  _1BIT_2_TO_1_MUX u_1bit_2_to_1_mux_7 (.DATA(DIN[6]), .DATA_2(DIN_2[6]), .SELECT(SELECT), .DOUT(DOUT[6]));
  _1BIT_2_TO_1_MUX u_1bit_2_to_1_mux_8 (.DATA(DIN[7]), .DATA_2(DIN_2[7]), .SELECT(SELECT), .DOUT(DOUT[7]));
endmodule

// MUX
module _1BIT_2_TO_1_MUX (
  input  SELECT,
  input  DATA,
  input  DATA_2,
  output DOUT
);

  wire and_1_out, and_2_out, not_1_out;

  not not_1 (not_1_out, SELECT);
  and and_1 (and_1_out, not_1_out, DATA);
  and and_2 (and_2_out, SELECT, DATA_2);
  or or_1 (DOUT, and_1_out, and_2_out);
endmodule

// GGPP
module GROUP_GENERATE_PROPAGATE (
  input  G0,
  input  P0,
  input  G1,
  input  P1,
  output GG01,
  output GP01
);

  wire and_1_out;

  and and_1 (and_1_out, G0, P1);
  or or_1 (GG01, and_1_out, G1);
  and and_2 (GP01, P0, P1);
endmodule

// GP
module GENERATE_PROPAGATE (
  input  A,
  input  B,
  output GG,
  output GP
);

  and and_1 (GG, A, B);
  xor xor_1 (GP, A, B);
endmodule

// AND
module _8BIT_AND (
  input  [7:0] A,
  input  [7:0] B,
  output [7:0] A_AND_B
);

  and and_1 (A_AND_B[0], A[0], B[0]);
  and and_2 (A_AND_B[1], A[1], B[1]);
  and and_3 (A_AND_B[2], A[2], B[2]);
  and and_4 (A_AND_B[3], A[3], B[3]);
  and and_5 (A_AND_B[4], A[4], B[4]);
  and and_6 (A_AND_B[5], A[5], B[5]);
  and and_7 (A_AND_B[6], A[6], B[6]);
  and and_8 (A_AND_B[7], A[7], B[7]);
endmodule

// OR
module _8BIT_OR (
  input  [7:0] A,
  input  [7:0] B,
  output [7:0] A_OR_B
);

  or or_1 (A_OR_B[0], A[0], B[0]);
  or or_2 (A_OR_B[1], A[1], B[1]);
  or or_3 (A_OR_B[2], A[2], B[2]);
  or or_4 (A_OR_B[3], A[3], B[3]);
  or or_5 (A_OR_B[4], A[4], B[4]);
  or or_6 (A_OR_B[5], A[5], B[5]);
  or or_7 (A_OR_B[6], A[6], B[6]);
  or or_8 (A_OR_B[7], A[7], B[7]);
endmodule

// NOT
module _8BIT_NOT (
  input  [7:0] IN,
  output [7:0] OUT
);

  not not_1 (OUT[0], IN[0]);
  not not_2 (OUT[1], IN[1]);
  not not_3 (OUT[2], IN[2]);
  not not_4 (OUT[3], IN[3]);
  not not_5 (OUT[4], IN[4]);
  not not_6 (OUT[5], IN[5]);
  not not_7 (OUT[6], IN[6]);
  not not_8 (OUT[7], IN[7]);
endmodule

// XOR
module _8BIT_XOR (
  input  [7:0] A,
  input  [7:0] B,
  output [7:0] A_XOR_B
);

  xor xor_1 (A_XOR_B[0], A[0], B[0]);
  xor xor_2 (A_XOR_B[1], A[1], B[1]);
  xor xor_3 (A_XOR_B[2], A[2], B[2]);
  xor xor_4 (A_XOR_B[3], A[3], B[3]);
  xor xor_5 (A_XOR_B[4], A[4], B[4]);
  xor xor_6 (A_XOR_B[5], A[5], B[5]);
  xor xor_7 (A_XOR_B[6], A[6], B[6]);
  xor xor_8 (A_XOR_B[7], A[7], B[7]);
endmodule

// SHFTL
module _8BIT_SHIFT_LEFT (
  input  [7:0] IN,
  output [7:0] OUT
);


  assign OUT = {IN[6:0], 1'b0};
endmodule

// SHFTR
module _8BIT_SHIFT_RIGHT (
  input  [7:0] IN,
  output [7:0] OUT
);


  assign OUT = {1'b0, IN[7:1]};
endmodule

// FA
module _1BIT_FULL_ADDER (
  input  Cin,
  input  A,
  input  B,
  output Sum,
  output Cout
);

  wire and_1_out, G_out, P_out;

  xor P (P_out, A, B);
  and G (G_out, A, B);
  xor xor_1 (Sum, Cin, P_out);
  and and_1 (and_1_out, P_out, Cin);
  or or_1 (Cout, and_1_out, G_out);

  // Notes on the sheet:
  //   CARRY = 3ms, SUM = 2ms (any logic gate = 1ms)
endmodule

// HA
module _1BIT_HALF_ADDER (
  input  A,
  input  B,
  output S,
  output C
);

  xor xor_1 (S, A, B);
  and and_1 (C, A, B);
endmodule

// INCR
module _8BIT_INCREMENT_RIPPLE (
  input  CIN__C0_1,
  input  [7:0] A0_A7,
  output [7:0] S0_S7,
  output COUT
);

  wire n1bit_half_adder_1_c, n1bit_half_adder_2_c, n1bit_half_adder_3_c, n1bit_half_adder_4_c,
       n1bit_half_adder_5_c, n1bit_half_adder_6_c, n1bit_half_adder_7_c;

  _1BIT_HALF_ADDER u_1bit_half_adder_1 (.A(A0_A7[0]), .B(CIN__C0_1), .S(S0_S7[0]), .C(n1bit_half_adder_1_c));
  _1BIT_HALF_ADDER u_1bit_half_adder_2 (.A(A0_A7[1]), .B(n1bit_half_adder_1_c), .S(S0_S7[1]), .C(n1bit_half_adder_2_c));
  _1BIT_HALF_ADDER u_1bit_half_adder_3 (.A(A0_A7[2]), .B(n1bit_half_adder_2_c), .S(S0_S7[2]), .C(n1bit_half_adder_3_c));
  _1BIT_HALF_ADDER u_1bit_half_adder_4 (.A(A0_A7[3]), .B(n1bit_half_adder_3_c), .S(S0_S7[3]), .C(n1bit_half_adder_4_c));
  _1BIT_HALF_ADDER u_1bit_half_adder_5 (.A(A0_A7[4]), .B(n1bit_half_adder_4_c), .S(S0_S7[4]), .C(n1bit_half_adder_5_c));
  _1BIT_HALF_ADDER u_1bit_half_adder_6 (.A(A0_A7[5]), .B(n1bit_half_adder_5_c), .S(S0_S7[5]), .C(n1bit_half_adder_6_c));
  _1BIT_HALF_ADDER u_1bit_half_adder_7 (.A(A0_A7[6]), .B(n1bit_half_adder_6_c), .S(S0_S7[6]), .C(n1bit_half_adder_7_c));
  _1BIT_HALF_ADDER u_1bit_half_adder_8 (.A(A0_A7[7]), .B(n1bit_half_adder_7_c), .S(S0_S7[7]), .C(COUT));
endmodule

// INCR
module _16BIT_INCREMENT_RIPPLE (
  input  [15:0] IN,
  output [15:0] OUT
);

  wire n8bit_increment_ripple_1_cout;

  _8BIT_INCREMENT_RIPPLE u_8bit_increment_ripple_1 (
    .A0_A7(IN[7:0]), .CIN__C0_1(1'b1), .COUT(n8bit_increment_ripple_1_cout), .S0_S7(OUT[7:0]));
  _8BIT_INCREMENT_RIPPLE u_8bit_increment_ripple_2 (
    .A0_A7(IN[15:8]), .CIN__C0_1(n8bit_increment_ripple_1_cout), .S0_S7(OUT[15:8]));  // open: COUT
endmodule

// DECR
module _8BIT_DECREMENT_RIPPLE (
  input  CIN__C0_0,
  input  [7:0] A0_A7,
  output [7:0] S0_S7,
  output COUT
);

  wire n1bit_decrement_1_cout, n1bit_decrement_2_cout, n1bit_decrement_3_cout, n1bit_decrement_4_cout,
       n1bit_decrement_5_cout, n1bit_decrement_6_cout, n1bit_decrement_7_cout;

  _1BIT_DECREMENT u_1bit_decrement_1 (.A(A0_A7[0]), .Cin(CIN__C0_0), .Sum(S0_S7[0]), .Cout(n1bit_decrement_1_cout));
  _1BIT_DECREMENT u_1bit_decrement_2 (
    .A(A0_A7[1]), .Cin(n1bit_decrement_1_cout), .Sum(S0_S7[1]), .Cout(n1bit_decrement_2_cout));
  _1BIT_DECREMENT u_1bit_decrement_3 (
    .A(A0_A7[2]), .Cin(n1bit_decrement_2_cout), .Sum(S0_S7[2]), .Cout(n1bit_decrement_3_cout));
  _1BIT_DECREMENT u_1bit_decrement_4 (
    .A(A0_A7[3]), .Cin(n1bit_decrement_3_cout), .Sum(S0_S7[3]), .Cout(n1bit_decrement_4_cout));
  _1BIT_DECREMENT u_1bit_decrement_5 (
    .A(A0_A7[4]), .Cin(n1bit_decrement_4_cout), .Sum(S0_S7[4]), .Cout(n1bit_decrement_5_cout));
  _1BIT_DECREMENT u_1bit_decrement_6 (
    .A(A0_A7[5]), .Cin(n1bit_decrement_5_cout), .Sum(S0_S7[5]), .Cout(n1bit_decrement_6_cout));
  _1BIT_DECREMENT u_1bit_decrement_7 (
    .A(A0_A7[6]), .Cin(n1bit_decrement_6_cout), .Sum(S0_S7[6]), .Cout(n1bit_decrement_7_cout));
  _1BIT_DECREMENT u_1bit_decrement_8 (.A(A0_A7[7]), .Cin(n1bit_decrement_7_cout), .Sum(S0_S7[7]), .Cout(COUT));
endmodule

// DECR
module _1BIT_DECREMENT (
  input  A,
  input  Cin,
  output Sum,
  output Cout
);

  wire and_1_out, not_1_out;

  not not_1 (not_1_out, A);
  xor xor_1 (Sum, Cin, not_1_out);
  and and_1 (and_1_out, Cin, not_1_out);
  or or_1 (Cout, and_1_out, A);
endmodule

// DECR
module _16BIT_DECREMENT_RIPPLE (
  input  [15:0] IN,
  output [15:0] OUT
);

  wire n8bit_decrement_ripple_1_cout;

  _8BIT_DECREMENT_RIPPLE u_8bit_decrement_ripple_1 (
    .A0_A7(IN[7:0]), .CIN__C0_0(1'b0), .COUT(n8bit_decrement_ripple_1_cout), .S0_S7(OUT[7:0]));
  _8BIT_DECREMENT_RIPPLE u_8bit_decrement_ripple_2 (
    .A0_A7(IN[15:8]), .CIN__C0_0(n8bit_decrement_ripple_1_cout), .S0_S7(OUT[15:8]));  // open: COUT
endmodule

// MUX
module _16BIT_4_TO_1_MUX (
  input  in_1,
  input  in_2,
  input  [15:0] DIN,
  input  [15:0] DIN_2,
  input  [15:0] DIN_3,
  input  [15:0] DIN_4,
  output [15:0] DOUT
);

  wire [7:0] n8bit_2_to_1_mux_1_dout, n8bit_2_to_1_mux_2_dout, n8bit_2_to_1_mux_3_dout,
       n8bit_2_to_1_mux_4_dout;

  _8BIT_2_TO_1_MUX u_8bit_2_to_1_mux_1 (
    .DIN(DIN[7:0]), .DIN_2(DIN_2[7:0]), .SELECT(in_1), .DOUT(n8bit_2_to_1_mux_1_dout));
  _8BIT_2_TO_1_MUX u_8bit_2_to_1_mux_2 (
    .DIN(DIN[15:8]), .DIN_2(DIN_2[15:8]), .SELECT(in_1), .DOUT(n8bit_2_to_1_mux_2_dout));
  _8BIT_2_TO_1_MUX u_8bit_2_to_1_mux_3 (
    .DIN(DIN_3[7:0]), .DIN_2(DIN_4[7:0]), .SELECT(in_1), .DOUT(n8bit_2_to_1_mux_3_dout));
  _8BIT_2_TO_1_MUX u_8bit_2_to_1_mux_4 (
    .DIN(DIN_3[15:8]), .DIN_2(DIN_4[15:8]), .SELECT(in_1), .DOUT(n8bit_2_to_1_mux_4_dout));
  _8BIT_2_TO_1_MUX u_8bit_2_to_1_mux_5 (
    .DIN(n8bit_2_to_1_mux_1_dout), .DIN_2(n8bit_2_to_1_mux_3_dout), .SELECT(in_2), .DOUT(DOUT[7:0]));
  _8BIT_2_TO_1_MUX u_8bit_2_to_1_mux_6 (
    .DIN(n8bit_2_to_1_mux_2_dout), .DIN_2(n8bit_2_to_1_mux_4_dout), .SELECT(in_2), .DOUT(DOUT[15:8]));
endmodule

// FLAG_CALC
module FLAG_SIGNALS (
  input  OP_SEL,
  input  [7:0] ALU_OUT,
  input  NON_ARITH_CARRY,
  input  ARITH_CARRY,
  input  C7,
  output [7:0] FLAGS
);

  wire xor_1_out;

  _8BIT_IS_ZERO u_8bit_is_zero_1 (.ALU_OUT(ALU_OUT), .OUT(FLAGS[0]));
  _1BIT_2_TO_1_MUX u_1bit_2_to_1_mux_1 (.DATA(ARITH_CARRY), .DATA_2(NON_ARITH_CARRY), .SELECT(OP_SEL), .DOUT(FLAGS[1]));
  xor xor_1 (xor_1_out, ARITH_CARRY, C7);
  _1BIT_2_TO_1_MUX u_1bit_2_to_1_mux_2 (.DATA(xor_1_out), .DATA_2(1'b0), .SELECT(OP_SEL), .DOUT(FLAGS[3]));

  assign {FLAGS[7:4], FLAGS[2]} = {4'b0000, ALU_OUT[7]};
endmodule

module ALU (
  input  [4:0] OPCODE,
  input  [7:0] A0_07,
  input  [7:0] B0_B7,
  output [7:0] ALU_OUT,
  output [7:0] FLAGS
);

  wire arithmetic_block_1_carry_flag, arithmetic_block_1_cin_bin_msb, shift_rotate_block_1_carry, xor_1_out;
  wire [7:0] arithmetic_block_1_sum_diff, logic_block_1_dout, shift_rotate_block_1_dout;

  ARITHMETIC_BLOCK arithmetic_block_1 (
    .A(A0_07), .B(B0_B7), .in_1(OPCODE[1]), .in_2(OPCODE[0]), .SUM_DIFF(arithmetic_block_1_sum_diff),
    .CARRY_FLAG(arithmetic_block_1_carry_flag), .CIN_BIN_MSB(arithmetic_block_1_cin_bin_msb));
  LOGIC_BLOCK logic_block_1 (
    .A0_07(A0_07), .B0_B7(B0_B7), .in_1(OPCODE[0]), .in_2(OPCODE[1]), .DOUT(logic_block_1_dout));
  SHIFT_ROTATE_BLOCK shift_rotate_block_1 (
    .A0_07(A0_07), .in_1(OPCODE[0]), .in_2(OPCODE[1]), .DOUT(shift_rotate_block_1_dout),
    .CARRY(shift_rotate_block_1_carry));
  _8BIT_4_TO_1_MUX u_8bit_4_to_1_mux_1 (
    .DIN(arithmetic_block_1_sum_diff), .DIN_2(logic_block_1_dout), .DIN_3(shift_rotate_block_1_dout),
    .DIN_4(arithmetic_block_1_sum_diff), .S0(OPCODE[2]), .S1(OPCODE[3]), .ALU_OUT(ALU_OUT));
  xor xor_1 (xor_1_out, OPCODE[2], OPCODE[3]);
  FLAG_SIGNALS flag_signals_1 (
    .ALU_OUT(ALU_OUT), .NON_ARITH_CARRY(shift_rotate_block_1_carry),
    .ARITH_CARRY(arithmetic_block_1_carry_flag), .C7(arithmetic_block_1_cin_bin_msb), .OP_SEL(xor_1_out),
    .FLAGS(FLAGS));
endmodule

// ARITHMETIC
module ARITHMETIC_BLOCK (
  input  in_1,
  input  in_2,
  input  [7:0] A,
  input  [7:0] B,
  output [7:0] SUM_DIFF,
  output CARRY_FLAG,
  output CIN_BIN_MSB
);

  wire [7:0] n8bit_2_to_1_mux_1_dout;

  _8BIT_2_TO_1_MUX u_8bit_2_to_1_mux_1 (.DIN(B), .DIN_2(8'h1), .SELECT(in_1), .DOUT(n8bit_2_to_1_mux_1_dout));
  _8BIT_ADDITION_SUBTRACTION_CIRCUIT u_8bit_addition_subtraction_circuit_1 (
    .A(A), .B(n8bit_2_to_1_mux_1_dout), .ADD_SUB_SIGNAL(in_2), .SUM_DIFF(SUM_DIFF), .COUT_BOUT(CARRY_FLAG),
    .CIN_BIN_MSB(CIN_BIN_MSB));
endmodule

// LOGIC
module LOGIC_BLOCK (
  input  in_1,
  input  in_2,
  input  [7:0] A0_07,
  input  [7:0] B0_B7,
  output [7:0] DOUT
);

  wire [7:0] n8bit_and_1_a_and_b, n8bit_not_1_out, n8bit_or_1_a_or_b, n8bit_xor_1_a_xor_b;

  _8BIT_AND u_8bit_and_1 (.A(A0_07), .B(B0_B7), .A_AND_B(n8bit_and_1_a_and_b));
  _8BIT_OR u_8bit_or_1 (.A(A0_07), .B(B0_B7), .A_OR_B(n8bit_or_1_a_or_b));
  _8BIT_NOT u_8bit_not_1 (.IN(A0_07), .OUT(n8bit_not_1_out));
  _8BIT_XOR u_8bit_xor_1 (.A(A0_07), .B(B0_B7), .A_XOR_B(n8bit_xor_1_a_xor_b));
  _8BIT_4_TO_1_MUX u_8bit_4_to_1_mux_1 (
    .DIN(n8bit_and_1_a_and_b), .DIN_2(n8bit_or_1_a_or_b), .DIN_3(n8bit_not_1_out),
    .DIN_4(n8bit_xor_1_a_xor_b), .S0(in_1), .S1(in_2), .ALU_OUT(DOUT));
endmodule

// SHFT/ROT
module SHIFT_ROTATE_BLOCK (
  input  in_1,
  input  in_2,
  input  [7:0] A0_07,
  output [7:0] DOUT,
  output CARRY
);

  wire not_1_out;
  wire [7:0] n8bit_rotate_left_1_out, n8bit_rotate_right_1_out, n8bit_shift_left_1_out,
       n8bit_shift_right_1_out;

  _8BIT_SHIFT_LEFT u_8bit_shift_left_1 (.IN(A0_07), .OUT(n8bit_shift_left_1_out));
  _8BIT_SHIFT_RIGHT u_8bit_shift_right_1 (.IN(A0_07), .OUT(n8bit_shift_right_1_out));
  _8BIT_ROTATE_LEFT u_8bit_rotate_left_1 (.IN(A0_07), .OUT(n8bit_rotate_left_1_out));
  _8BIT_ROTATE_RIGHT u_8bit_rotate_right_1 (.IN(A0_07), .OUT(n8bit_rotate_right_1_out));
  _8BIT_4_TO_1_MUX u_8bit_4_to_1_mux_1 (
    .DIN(n8bit_shift_left_1_out), .DIN_2(n8bit_shift_right_1_out), .DIN_3(n8bit_rotate_left_1_out),
    .DIN_4(n8bit_rotate_right_1_out), .S0(in_1), .S1(in_2), .ALU_OUT(DOUT));
  not not_1 (not_1_out, in_1);
  _1BIT_2_TO_1_MUX u_1bit_2_to_1_mux_1 (.DATA(A0_07[0]), .DATA_2(A0_07[7]), .SELECT(not_1_out), .DOUT(CARRY));
endmodule

// ROTL
module _8BIT_ROTATE_LEFT (
  input  [7:0] IN,
  output [7:0] OUT
);


  assign OUT = {IN[6:0], IN[7]};
endmodule

// ROTR
module _8BIT_ROTATE_RIGHT (
  input  [7:0] IN,
  output [7:0] OUT
);


  assign OUT = {IN[0], IN[7:1]};
endmodule

// ZERO
module _8BIT_IS_ZERO (
  input  [7:0] ALU_OUT,
  output OUT
);

  wire or_1_out, or_2_out, or_3_out, or_4_out, or_5_out, or_6_out, or_7_out;

  or or_1 (or_1_out, ALU_OUT[0], ALU_OUT[1]);
  or or_2 (or_2_out, ALU_OUT[2], ALU_OUT[3]);
  or or_3 (or_3_out, ALU_OUT[4], ALU_OUT[5]);
  or or_4 (or_4_out, ALU_OUT[6], ALU_OUT[7]);
  or or_5 (or_5_out, or_1_out, or_2_out);
  or or_6 (or_6_out, or_3_out, or_4_out);
  or or_7 (or_7_out, or_5_out, or_6_out);
  not not_1 (OUT, or_7_out);
endmodule
