// Logisim project 8BIT_CPU.circ as structural Verilog: 14 circuits, main circuit CPU_WITH_IO
// CPU_01
module CPU_WITH_IO (
  input  RESET,
  output [7:0] STATE,
  output [15:0] PC,
  output [4:0] OPCODE
);

  wire and_1_out, and_2_out, CLOCK_out, d_flip_flop_with_write_enable_1_q, io_unit_1_display_enable,
       io_unit_1_io_sel, io_unit_1_keyboard_enable, io_unit_1_mar_we_2, io_unit_1_mdr_we_2,
       io_unit_1_mem_rd_2, io_unit_1_mem_wr_2, keyboard_1_avail, not_1_out, not_2_out;
  wire [1:0] control_unit_1_signals_bottom_2, control_unit_1_signals_top_2, fetch_unit_1_ir_out;
  wire [2:0] fetch_unit_1_ir_out_2, fetch_unit_1_ir_out_3, fetch_unit_1_ir_out_4;
  wire [6:0] keyboard_1_data, n8bit_2_to_1_mux_1_dout;
  wire [7:0] alu_1_alu_out, alu_1_flags, data_memory_unit_1_mdr_out, flag_register_1_out,
       io_unit_1_io_data_out, n8_register_file_1_read_a, n8_register_file_1_read_b, n8bit_2_to_1_mux_2_dout,
       temporary_register_unit_1_to_mdr_mux;
  wire [7:7] n8bit_2_to_1_mux_1_dout_2;
  wire [9:0] control_unit_1_signals_bottom;
  wire [11:0] control_unit_1_signals_top;
  wire [15:0] fetch_unit_1_immd_out, stack_pointer_unit_1_stack_out, temporary_register_unit_1_to_pc;

  D_FLIP_FLOP_WITH_WRITE_ENABLE d_flip_flop_with_write_enable_1 (
    .D(1'b1), .WE(control_unit_1_signals_top[11]), .CLOCK(CLOCK_out), .RESET(RESET),
    .Q(d_flip_flop_with_write_enable_1_q));
  not not_1 (not_1_out, d_flip_flop_with_write_enable_1_q);
  FETCH_UNIT fetch_unit_1 (
    .TEMP_REG(temporary_register_unit_1_to_pc), .PC_MUX(control_unit_1_signals_bottom_2),
    .PC_WE(control_unit_1_signals_bottom[9]), .CLK(and_1_out), .RESET(RESET),
    .IR_WE(control_unit_1_signals_bottom[8]), .IMMD_REG_WE(control_unit_1_signals_bottom[7]),
    .IR_OUT({OPCODE, fetch_unit_1_ir_out_2, fetch_unit_1_ir_out_3, fetch_unit_1_ir_out_4, fetch_unit_1_ir_out}),
    .IMMD_OUT(fetch_unit_1_immd_out), .PC(PC));
  and and_1 (and_1_out, CLOCK_out, not_1_out);
  CONTROL_UNIT control_unit_1 (
    .FROM_IR({OPCODE, fetch_unit_1_ir_out_2, fetch_unit_1_ir_out_3, fetch_unit_1_ir_out_4, fetch_unit_1_ir_out}),
    .FROM_FR(flag_register_1_out), .CLK(and_1_out), .RESET(RESET), .CURR_STATE(STATE),
    .SIGNALS_TOP({control_unit_1_signals_top[11:4], control_unit_1_signals_top_2, control_unit_1_signals_top[1:0]}),
    .SIGNALS_BOTTOM({control_unit_1_signals_bottom_2, control_unit_1_signals_bottom}));  // open: NEXT_STATE
  TEMPORARY_REGISTER_UNIT temporary_register_unit_1 (
    .FROM_PC(PC), .FROM_MDR(data_memory_unit_1_mdr_out), .TEMP_SRC(control_unit_1_signals_bottom[6]),
    .TEMP_H_WE(control_unit_1_signals_bottom[5]), .TEMP_L_WE(control_unit_1_signals_bottom[4]),
    .CLK(and_1_out), .RESET(RESET), .TEMP_LH_SEL(control_unit_1_signals_bottom[3]),
    .TO_PC(temporary_register_unit_1_to_pc), .TO_MDR_MUX(temporary_register_unit_1_to_mdr_mux));
  STACK_POINTER_UNIT stack_pointer_unit_1 (
    .SP_SEL(control_unit_1_signals_bottom[2:1]), .SP_WE(control_unit_1_signals_bottom[0]), .CLK(and_1_out),
    .RESET(RESET), .STACK_OUT(stack_pointer_unit_1_stack_out));
  not not_2 (not_2_out, control_unit_1_signals_top[9]);
  and and_2 (and_2_out, not_2_out, control_unit_1_signals_top[8]);
  _8BIT_2_TO_1_MUX u_8bit_2_to_1_mux_1 (
    .DIN({fetch_unit_1_ir_out_3, fetch_unit_1_ir_out_4, fetch_unit_1_ir_out}),
    .DIN_2(n8_register_file_1_read_a), .SELECT(and_2_out),
    .DOUT({n8bit_2_to_1_mux_1_dout_2[7], n8bit_2_to_1_mux_1_dout}));
  IO_UNIT io_unit_1 (
    .MAR_WE(control_unit_1_signals_top[4]), .MDR_WE(control_unit_1_signals_top[5]),
    .MEM_RD(control_unit_1_signals_top[6]), .MEM_WR(control_unit_1_signals_top[7]),
    .FROM_IMMD(fetch_unit_1_immd_out), .KEY_DATA({1'b0, keyboard_1_data}), .KEY_AVAIL(keyboard_1_avail),
    .CLK(and_1_out), .RESET(RESET), .MAR_WE_2(io_unit_1_mar_we_2), .MDR_WE_2(io_unit_1_mdr_we_2),
    .MEM_RD_2(io_unit_1_mem_rd_2), .MEM_WR_2(io_unit_1_mem_wr_2), .IO_SEL(io_unit_1_io_sel),
    .DISPLAY_ENABLE(io_unit_1_display_enable), .KEYBOARD_ENABLE(io_unit_1_keyboard_enable),
    .IO_DATA_OUT(io_unit_1_io_data_out));
  Keyboard keyboard_1 (
    .clk(and_1_out), .re(io_unit_1_keyboard_enable), .clr(RESET), .avail(keyboard_1_avail),
    .data(keyboard_1_data));
  DATA_MEMORY_UNIT data_memory_unit_1 (
    .IMM_DATA({fetch_unit_1_ir_out_3, fetch_unit_1_ir_out_4, fetch_unit_1_ir_out}),
    .REG_A(n8_register_file_1_read_a), .TEMP_REG_LH(temporary_register_unit_1_to_mdr_mux),
    .IMMD_OUT(fetch_unit_1_immd_out), .SP_OUT(stack_pointer_unit_1_stack_out),
    .MAR_MUX(control_unit_1_signals_top[10]), .MDR_MUX(control_unit_1_signals_top[9:8]),
    .MAR_WE(io_unit_1_mem_wr_2), .MDR_WE(io_unit_1_mem_rd_2), .MEM_RD(io_unit_1_mdr_we_2),
    .MEM_WR(io_unit_1_mar_we_2), .CLK(and_1_out), .RESET(RESET), .MDR_OUT(data_memory_unit_1_mdr_out));
  _8BIT_2_TO_1_MUX u_8bit_2_to_1_mux_2 (
    .DIN(data_memory_unit_1_mdr_out), .DIN_2(io_unit_1_io_data_out), .SELECT(io_unit_1_io_sel),
    .DOUT(n8bit_2_to_1_mux_2_dout));
  _8_REGISTER_FILE u_8_register_file_1 (
    .IMM_DATA({fetch_unit_1_ir_out_3, fetch_unit_1_ir_out_4, fetch_unit_1_ir_out}),
    .MDR_OUT(n8bit_2_to_1_mux_2_dout), .ALU_OUT(alu_1_alu_out), .REG_MUX(control_unit_1_signals_top_2),
    .WRITE_SELECT(fetch_unit_1_ir_out_2), .REG_WE(control_unit_1_signals_top[1]), .CLK(and_1_out),
    .RESET(RESET), .A_SELECT(fetch_unit_1_ir_out_3), .B_SELECT(fetch_unit_1_ir_out_4),
    .READ_A(n8_register_file_1_read_a), .READ_B(n8_register_file_1_read_b));
  TTY tty_1 (.data(n8bit_2_to_1_mux_1_dout), .clk(and_1_out), .we(io_unit_1_display_enable), .clr(RESET));
  ALU alu_1 (
    .A0_07(n8_register_file_1_read_a), .B0_B7(n8_register_file_1_read_b), .OPCODE(OPCODE),
    .ALU_OUT(alu_1_alu_out), .FLAGS(alu_1_flags));
  FLAG_REGISTER flag_register_1 (
    .IN(alu_1_flags), .FLAG_WE(control_unit_1_signals_top[0]), .CLK(and_1_out), .RESET(RESET),
    .OUT(flag_register_1_out));
  Clock CLOCK (.out(CLOCK_out));

  // Notes on the sheet:
  //   SCROLL DOWN TO OPERATE
endmodule

// FETCH
module FETCH_UNIT (
  input  [1:0] PC_MUX,
  input  PC_WE,
  input  CLK,
  input  RESET,
  input  IR_WE,
  input  IMMD_REG_WE,
  input  [15:0] TEMP_REG,
  output [15:0] IR_OUT,
  output [15:0] IMMD_OUT,
  output [15:0] PC
);

  wire [15:0] n16bit_4_to_1_mux_1_dout, n16bit_increment_ripple_1_out, ram_1_data;

  _16BIT_4_TO_1_MUX u_16bit_4_to_1_mux_1 (
    .DIN(n16bit_increment_ripple_1_out), .DIN_2(IMMD_OUT), .DIN_3(TEMP_REG), .in_1(PC_MUX[0]),
    .in_2(PC_MUX[1]), .DOUT(n16bit_4_to_1_mux_1_dout));  // open: DIN_4
  _16BIT_REGISTER u_PC (.DIN(n16bit_4_to_1_mux_1_dout), .WE(PC_WE), .CLK(CLK), .RESET(RESET), .DOUT(PC));
  _16BIT_INCREMENT_RIPPLE u_16bit_increment_ripple_1 (.IN(PC), .OUT(n16bit_increment_ripple_1_out));
  RAM #(.addrWidth(16), .dataWidth(16)) ram_1 (
    .addr(PC), .data(ram_1_data), .sel(1'b1), .clk(CLK), .ld(1'b1), .clr(1'b0));
  _16BIT_REGISTER IR (.DIN(ram_1_data), .WE(IR_WE), .CLK(CLK), .RESET(RESET), .DOUT(IR_OUT));
  _16BIT_REGISTER IMMD (.DIN(ram_1_data), .WE(IMMD_REG_WE), .CLK(CLK), .RESET(RESET), .DOUT(IMMD_OUT));
endmodule

// TEMP
module TEMPORARY_REGISTER_UNIT (
  input  TEMP_SRC,
  input  TEMP_H_WE,
  input  TEMP_L_WE,
  input  CLK,
  input  RESET,
  input  TEMP_LH_SEL,
  input  [15:0] FROM_PC,
  input  [7:0] FROM_MDR,
  output [15:0] TO_PC,
  output [7:0] TO_MDR_MUX
);

  wire [7:0] n8bit_2_to_1_mux_1_dout, n8bit_2_to_1_mux_2_dout;

  _8BIT_2_TO_1_MUX u_8bit_2_to_1_mux_1 (
    .DIN(FROM_PC[7:0]), .DIN_2(FROM_MDR), .SELECT(TEMP_SRC), .DOUT(n8bit_2_to_1_mux_1_dout));
  _8BIT_2_TO_1_MUX u_8bit_2_to_1_mux_2 (
    .DIN(FROM_PC[15:8]), .DIN_2(FROM_MDR), .SELECT(TEMP_SRC), .DOUT(n8bit_2_to_1_mux_2_dout));
  _8BIT_REGISTER u_8bit_register_1 (
    .DIN(n8bit_2_to_1_mux_2_dout), .WE(TEMP_H_WE), .CLK(CLK), .RESET(RESET), .DOUT(TO_PC[15:8]));
  _8BIT_REGISTER u_8bit_register_2 (
    .DIN(n8bit_2_to_1_mux_1_dout), .WE(TEMP_L_WE), .CLK(CLK), .RESET(RESET), .DOUT(TO_PC[7:0]));
  _8BIT_2_TO_1_MUX u_8bit_2_to_1_mux_3 (.DIN(TO_PC[7:0]), .DIN_2(TO_PC[15:8]), .SELECT(TEMP_LH_SEL), .DOUT(TO_MDR_MUX));
endmodule

// DMU
module DATA_MEMORY_UNIT (
  input  MAR_MUX,
  input  [1:0] MDR_MUX,
  input  MAR_WE,
  input  MDR_WE,
  input  MEM_RD,
  input  MEM_WR,
  input  CLK,
  input  RESET,
  input  [7:0] IMM_DATA,
  input  [7:0] REG_A,
  input  [7:0] TEMP_REG_LH,
  input  [15:0] IMMD_OUT,
  input  [15:0] SP_OUT,
  output [7:0] MDR_OUT
);

  wire [7:0] n8bit_4_to_1_mux_1_alu_out, ram_1_data;
  wire [15:0] n16bit_2_to_1_mux_1_dout, n16bit_register_1_dout;

  _16BIT_2_TO_1_MUX u_16bit_2_to_1_mux_1 (
    .DIN(IMMD_OUT), .DIN_2(SP_OUT), .in_1(MAR_MUX), .DOUT(n16bit_2_to_1_mux_1_dout));
  _16BIT_REGISTER u_16bit_register_1 (
    .DIN(n16bit_2_to_1_mux_1_dout), .WE(MAR_WE), .CLK(CLK), .RESET(RESET), .DOUT(n16bit_register_1_dout));
  RAM #(.addrWidth(16), .bus("separate")) ram_1 (
    .addr(n16bit_register_1_dout), .din(MDR_OUT), .data(ram_1_data), .str(MEM_WR), .sel(1'b1), .clk(CLK),
    .ld(MEM_RD), .clr(RESET));
  _8BIT_4_TO_1_MUX u_8bit_4_to_1_mux_1 (
    .DIN(IMM_DATA), .DIN_2(REG_A), .DIN_3(ram_1_data), .DIN_4(TEMP_REG_LH), .S0(MDR_MUX[0]), .S1(MDR_MUX[1]),
    .ALU_OUT(n8bit_4_to_1_mux_1_alu_out));
  _8BIT_REGISTER u_8bit_register_1 (
    .DIN(n8bit_4_to_1_mux_1_alu_out), .WE(MDR_WE), .CLK(CLK), .RESET(RESET), .DOUT(MDR_OUT));
endmodule

// SP
module STACK_POINTER_UNIT (
  input  [1:0] SP_SEL,
  input  SP_WE,
  input  CLK,
  input  RESET,
  output [15:0] STACK_OUT
);

  wire [15:0] n16bit_4_to_1_mux_1_dout, n16bit_decrement_ripple_1_out, n16bit_increment_ripple_1_out;

  _16BIT_4_TO_1_MUX u_16bit_4_to_1_mux_1 (
    .DIN(n16bit_increment_ripple_1_out), .DIN_2(n16bit_decrement_ripple_1_out), .DIN_3({16{1'b1}}),
    .DIN_4({16{1'b1}}), .in_1(SP_SEL[0]), .in_2(SP_SEL[1]), .DOUT(n16bit_4_to_1_mux_1_dout));
  _16BIT_REGISTER u_16bit_register_1 (
    .DIN(n16bit_4_to_1_mux_1_dout), .WE(SP_WE), .CLK(CLK), .RESET(RESET), .DOUT(STACK_OUT));
  _16BIT_INCREMENT_RIPPLE u_16bit_increment_ripple_1 (.IN(STACK_OUT), .OUT(n16bit_increment_ripple_1_out));
  _16BIT_DECREMENT_RIPPLE u_16bit_decrement_ripple_1 (.IN(STACK_OUT), .OUT(n16bit_decrement_ripple_1_out));
endmodule

// SM
module STATE_MACHINE (
  input  CLK,
  input  RESET,
  input  STATE_RESET,
  output TINIT,
  output T0,
  output T1,
  output T2,
  output T3,
  output T4,
  output T5,
  output T6,
  output T7,
  output T8,
  output T9,
  output [7:0] CURRENT_STATE,
  output [7:0] NEXT_STATE
);

  wire [7:0] n8bit_increment_ripple_1_s0_s7;
  wire [15:11] n4_to_16_decoder_1_out;

  _8BIT_REGISTER u_8bit_register_1 (.DIN(NEXT_STATE), .WE(1'b1), .CLK(CLK), .RESET(RESET), .DOUT(CURRENT_STATE));
  _8BIT_INCREMENT_RIPPLE u_8bit_increment_ripple_1 (
    .A0_A7(CURRENT_STATE), .CIN__C0_1(1'b1), .S0_S7(n8bit_increment_ripple_1_s0_s7));  // open: COUT
  _8BIT_2_TO_1_MUX u_8bit_2_to_1_mux_1 (
    .DIN(n8bit_increment_ripple_1_s0_s7), .DIN_2(8'h1), .SELECT(STATE_RESET), .DOUT(NEXT_STATE));
  _4_TO_16_DECODER u_4_to_16_decoder_1 (
    .S3(CURRENT_STATE[3]), .S2(CURRENT_STATE[2]), .S1(CURRENT_STATE[1]), .S0(CURRENT_STATE[0]),
    .OUT({n4_to_16_decoder_1_out, T9, T8, T7, T6, T5, T4, T3, T2, T1, T0, TINIT}));
endmodule

// FLAG_REG
module FLAG_REGISTER (
  input  FLAG_WE,
  input  CLK,
  input  RESET,
  input  [7:0] IN,
  output [7:0] OUT
);

  _8BIT_REGISTER u_8bit_register_1 (.DIN(IN), .WE(FLAG_WE), .CLK(CLK), .RESET(RESET), .DOUT(OUT));
endmodule

// ODU
module OPCODE_DECODE_UNIT (
  input  [7:0] FROM_FR,
  input  [4:0] OPCODE,
  output BRANCH_TAKEN,
  output CMP,
  output RESERVED,
  output ALU_GROUP,
  output BRANCH_GROUP,
  output JMP,
  output CALL,
  output RET,
  output HALT,
  output PUSH,
  output POP,
  output MOVI,
  output MOV,
  output LOAD,
  output STORE,
  output STOREI,
  output NOP,
  output MOV_GROUP,
  output STORE_GROUP
);

  wire and_1_out, and_2_out, and_3_out, and_4_out, and_5_out, and_7_out, and_8_out, and_9_out, and_10_out,
       and_11_out, and_12_out, and_13_out, and_14_out, and_15_out, and_16_out, and_17_out, and_18_out,
       and_19_out, and_21_out, and_22_out, and_23_out, and_24_out, and_25_out, and_26_out, and_27_out,
       and_28_out, and_29_out, and_30_out, and_31_out, and_32_out, and_47_out, and_48_out, and_49_out,
       and_50_out, and_51_out, not_1_out, not_2_out, not_3_out, not_4_out, not_5_out, not_6_out, not_7_out,
       not_8_out, not_9_out, not_10_out, not_11_out, not_12_out, not_13_out, not_14_out, not_15_out,
       not_16_out, not_17_out, not_18_out, or_1_out, or_2_out, xor_1_out;

  and and_1 (and_1_out, OPCODE[4], OPCODE[3]);
  not not_1 (not_1_out, OPCODE[2]);
  not not_2 (not_2_out, OPCODE[1]);
  and and_2 (and_2_out, OPCODE[2], OPCODE[3]);
  not not_3 (not_3_out, OPCODE[4]);
  and and_3 (and_3_out, OPCODE[4], OPCODE[3]);
  not not_4 (not_4_out, OPCODE[3]);
  not not_5 (not_5_out, OPCODE[3]);
  not not_6 (not_6_out, OPCODE[0]);
  not not_7 (not_7_out, OPCODE[1]);
  not not_8 (not_8_out, OPCODE[0]);
  not not_9 (not_9_out, OPCODE[1]);
  and and_4 (and_4_out, OPCODE[4], not_4_out);
  and and_5 (and_5_out, OPCODE[4], not_5_out);
  and and_6 (BRANCH_GROUP, and_1_out, not_1_out);
  and and_7 (and_7_out, not_2_out, OPCODE[0]);
  and and_8 (and_8_out, and_2_out, not_3_out);
  not not_10 (not_10_out, and_2_out);
  and and_9 (and_9_out, and_3_out, OPCODE[2]);
  not not_11 (not_11_out, OPCODE[2]);
  not not_12 (not_12_out, OPCODE[0]);
  not not_13 (not_13_out, OPCODE[1]);
  not not_14 (not_14_out, OPCODE[0]);
  not not_15 (not_15_out, OPCODE[1]);
  and and_10 (and_10_out, not_6_out, not_7_out);
  and and_11 (and_11_out, OPCODE[0], not_7_out);
  and and_12 (and_12_out, not_6_out, OPCODE[1]);
  and and_13 (and_13_out, OPCODE[0], OPCODE[1]);
  and and_14 (and_14_out, not_8_out, not_9_out);
  and and_15 (and_15_out, OPCODE[0], not_9_out);
  and and_16 (and_16_out, not_8_out, OPCODE[1]);
  and and_17 (and_17_out, OPCODE[0], OPCODE[1]);
  and and_18 (and_18_out, and_4_out, not_11_out);
  and and_19 (and_19_out, and_5_out, OPCODE[2]);
  not not_16 (not_16_out, and_7_out);
  and and_20 (ALU_GROUP, not_10_out, not_3_out);
  and and_21 (and_21_out, not_12_out, not_13_out);
  and and_22 (and_22_out, OPCODE[0], not_13_out);
  and and_23 (and_23_out, not_12_out, OPCODE[1]);
  and and_24 (and_24_out, OPCODE[0], OPCODE[1]);
  and and_25 (and_25_out, not_14_out, not_15_out);
  and and_26 (and_26_out, OPCODE[0], not_15_out);
  and and_27 (and_27_out, not_14_out, OPCODE[1]);
  and and_28 (and_28_out, OPCODE[0], OPCODE[1]);
  and and_29 (and_29_out, BRANCH_GROUP, and_10_out);
  and and_30 (and_30_out, BRANCH_GROUP, and_11_out);
  and and_31 (and_31_out, BRANCH_GROUP, and_12_out);
  and and_32 (and_32_out, BRANCH_GROUP, and_13_out);
  and and_33 (CMP, and_8_out, and_7_out);
  and and_34 (JMP, and_9_out, and_14_out);
  and and_35 (CALL, and_9_out, and_15_out);
  and and_36 (RET, and_9_out, and_16_out);
  and and_37 (HALT, and_9_out, and_17_out);
  and and_38 (RESERVED, not_16_out, and_8_out);
  and and_39 (PUSH, and_18_out, and_21_out);
  and and_40 (POP, and_18_out, and_22_out);
  and and_41 (MOVI, and_18_out, and_23_out);
  and and_42 (MOV, and_18_out, and_24_out);
  and and_43 (LOAD, and_19_out, and_25_out);
  and and_44 (STORE, and_19_out, and_26_out);
  and and_45 (STOREI, and_19_out, and_27_out);
  and and_46 (NOP, and_19_out, and_28_out);
  not not_17 (not_17_out, FROM_FR[0]);
  and and_47 (and_47_out, FROM_FR[0], and_29_out);
  and and_48 (and_48_out, not_17_out, and_30_out);
  xor xor_1 (xor_1_out, FROM_FR[2], FROM_FR[3]);
  not not_18 (not_18_out, xor_1_out);
  or or_1 (or_1_out, and_47_out, and_48_out);
  and and_49 (and_49_out, xor_1_out, and_31_out);
  and and_50 (and_50_out, not_18_out, not_17_out);
  and and_51 (and_51_out, and_50_out, and_32_out);
  or or_2 (or_2_out, and_49_out, and_51_out);
  or or_3 (MOV_GROUP, MOVI, MOV);
  or or_4 (STORE_GROUP, STORE, STOREI);
  or or_5 (BRANCH_TAKEN, or_1_out, or_2_out);

  // Notes on the sheet:
  //   BY - @VENUDAYYAM
endmodule

// OGU
module OPCODE_GROUPING_UNIT (
  input  [7:0] FROM_FR,
  input  [4:0] OPCODE,
  output CMP___ALU_G,
  output JMP___BRANCH_G,
  output CALL___RET,
  output ALU_G___MOV_G,
  output LOAD___PUSH,
  output CALL___LOAD,
  output STORE_G___POP,
  output RET___POP,
  output IMMD_T1,
  output MAR_T2,
  output MDR_T2,
  output RESERVE___HALT,
  output NOP
);

  wire opcode_decode_unit_1_alu_group, opcode_decode_unit_1_branch_group, opcode_decode_unit_1_call,
       opcode_decode_unit_1_cmp, opcode_decode_unit_1_halt, opcode_decode_unit_1_jmp,
       opcode_decode_unit_1_load, opcode_decode_unit_1_mov_group, opcode_decode_unit_1_pop,
       opcode_decode_unit_1_push, opcode_decode_unit_1_reserved, opcode_decode_unit_1_ret,
       opcode_decode_unit_1_store_group, or_9_out;

  OPCODE_DECODE_UNIT opcode_decode_unit_1 (
    .FROM_FR(FROM_FR), .OPCODE(OPCODE), .CMP(opcode_decode_unit_1_cmp),
    .RESERVED(opcode_decode_unit_1_reserved), .ALU_GROUP(opcode_decode_unit_1_alu_group),
    .BRANCH_GROUP(opcode_decode_unit_1_branch_group), .JMP(opcode_decode_unit_1_jmp),
    .CALL(opcode_decode_unit_1_call), .RET(opcode_decode_unit_1_ret), .HALT(opcode_decode_unit_1_halt),
    .PUSH(opcode_decode_unit_1_push), .POP(opcode_decode_unit_1_pop), .LOAD(opcode_decode_unit_1_load),
    .NOP(NOP), .MOV_GROUP(opcode_decode_unit_1_mov_group), .STORE_GROUP(opcode_decode_unit_1_store_group));  // open: BRANCH_TAKEN, MOVI, MOV, STORE, STOREI
  or or_1 (CMP___ALU_G, opcode_decode_unit_1_cmp, opcode_decode_unit_1_alu_group);
  or or_2 (JMP___BRANCH_G, opcode_decode_unit_1_branch_group, opcode_decode_unit_1_jmp);
  or or_3 (CALL___RET, opcode_decode_unit_1_call, opcode_decode_unit_1_ret);
  or or_4 (ALU_G___MOV_G, opcode_decode_unit_1_alu_group, opcode_decode_unit_1_mov_group);
  or or_5 (LOAD___PUSH, opcode_decode_unit_1_load, opcode_decode_unit_1_push);
  or or_6 (CALL___LOAD, opcode_decode_unit_1_call, opcode_decode_unit_1_load);
  or or_7 (STORE_G___POP, opcode_decode_unit_1_pop, opcode_decode_unit_1_store_group);
  or or_8 (RET___POP, opcode_decode_unit_1_ret, opcode_decode_unit_1_pop);
  or or_9 (or_9_out, JMP___BRANCH_G, CALL___LOAD);
  or or_10 (MAR_T2, LOAD___PUSH, opcode_decode_unit_1_store_group);
  or or_11 (MDR_T2, opcode_decode_unit_1_store_group, RET___POP);
  or or_12 (RESERVE___HALT, opcode_decode_unit_1_halt, opcode_decode_unit_1_reserved);
  or or_13 (IMMD_T1, or_9_out, opcode_decode_unit_1_store_group);

  // Notes on the sheet:
  //   JMP + BRANCH_G
  //   CALL + RET
  //   ALU_G + MOV_G
  //   LOAD + PUSH
  //   CALL + LOAD
  //   STORE_G + POP
  //   RET + POP
  //   CMP + ALU_G
  //   IMMD_T1
  //   MAR_T2
  //   MDR_T2
endmodule

// CU
module CONTROL_UNIT (
  input  CLK,
  input  RESET,
  input  [15:0] FROM_IR,
  input  [7:0] FROM_FR,
  output [7:0] CURR_STATE,
  output [7:0] NEXT_STATE,
  output [11:0] SIGNALS_TOP,
  output [11:0] SIGNALS_BOTTOM
);

  wire and_1_out, and_2_out, and_3_out, and_4_out, and_5_out, and_6_out, and_7_out, and_9_out, and_10_out,
       and_11_out, and_12_out, and_13_out, and_14_out, and_15_out, and_18_out, and_19_out, and_20_out,
       and_21_out, and_22_out, and_23_out, and_24_out, and_25_out, and_26_out, and_27_out, and_28_out,
       and_29_out, and_30_out, and_31_out, and_33_out, and_34_out, and_36_out, and_37_out, and_38_out,
       and_39_out, and_40_out, and_41_out, and_42_out, and_43_out, and_44_out, and_45_out, and_46_out,
       and_47_out, and_48_out, and_49_out, and_50_out, and_51_out, and_53_out, and_55_out, and_56_out,
       and_57_out, opcode_decode_unit_1_alu_group, opcode_decode_unit_1_branch_taken,
       opcode_decode_unit_1_call, opcode_decode_unit_1_jmp, opcode_decode_unit_1_load,
       opcode_decode_unit_1_mov, opcode_decode_unit_1_mov_group, opcode_decode_unit_1_pop,
       opcode_decode_unit_1_push, opcode_decode_unit_1_ret, opcode_decode_unit_1_store,
       opcode_decode_unit_1_store_group, opcode_grouping_unit_1_alu_g___mov_g,
       opcode_grouping_unit_1_call___load, opcode_grouping_unit_1_call___ret,
       opcode_grouping_unit_1_cmp___alu_g, opcode_grouping_unit_1_immd_t1,
       opcode_grouping_unit_1_jmp___branch_g, opcode_grouping_unit_1_mar_t2, opcode_grouping_unit_1_mdr_t2,
       opcode_grouping_unit_1_nop, opcode_grouping_unit_1_reserve___halt, opcode_grouping_unit_1_ret___pop,
       opcode_grouping_unit_1_store_g___pop, or_1_out, or_2_out, or_3_out, or_4_out, or_5_out, or_6_out,
       or_7_out, or_8_out, or_9_out, or_10_out, or_11_out, or_12_out, or_13_out, or_14_out, or_15_out,
       or_16_out, or_17_out, or_18_out, or_19_out, or_20_out, or_21_out, or_22_out, or_23_out, or_27_out,
       or_28_out, or_29_out, or_30_out, or_31_out, or_32_out, or_33_out, or_36_out, or_37_out, or_38_out,
       or_42_out, or_45_out, or_46_out, or_50_out, state_machine_1_t1, state_machine_1_t2,
       state_machine_1_t3, state_machine_1_t4, state_machine_1_t5, state_machine_1_t6, state_machine_1_t7;

  STATE_MACHINE state_machine_1 (
    .CLK(CLK), .RESET(RESET), .STATE_RESET(or_50_out), .TINIT(SIGNALS_BOTTOM[2]), .T0(SIGNALS_BOTTOM[8]),
    .T1(state_machine_1_t1), .T2(state_machine_1_t2), .T3(state_machine_1_t3), .T4(state_machine_1_t4),
    .T5(state_machine_1_t5), .T6(state_machine_1_t6), .T7(state_machine_1_t7), .CURRENT_STATE(CURR_STATE),
    .NEXT_STATE(NEXT_STATE));  // open: T8, T9
  OPCODE_DECODE_UNIT opcode_decode_unit_1 (
    .FROM_FR(FROM_FR), .OPCODE(FROM_IR[15:11]), .BRANCH_TAKEN(opcode_decode_unit_1_branch_taken),
    .ALU_GROUP(opcode_decode_unit_1_alu_group), .JMP(opcode_decode_unit_1_jmp),
    .CALL(opcode_decode_unit_1_call), .RET(opcode_decode_unit_1_ret), .PUSH(opcode_decode_unit_1_push),
    .POP(opcode_decode_unit_1_pop), .MOV(opcode_decode_unit_1_mov), .LOAD(opcode_decode_unit_1_load),
    .STORE(opcode_decode_unit_1_store), .MOV_GROUP(opcode_decode_unit_1_mov_group),
    .STORE_GROUP(opcode_decode_unit_1_store_group));  // open: CMP, RESERVED, BRANCH_GROUP, HALT, MOVI, STOREI, NOP
  OPCODE_GROUPING_UNIT opcode_grouping_unit_1 (
    .FROM_FR(FROM_FR), .OPCODE(FROM_IR[15:11]), .CMP___ALU_G(opcode_grouping_unit_1_cmp___alu_g),
    .JMP___BRANCH_G(opcode_grouping_unit_1_jmp___branch_g), .CALL___RET(opcode_grouping_unit_1_call___ret),
    .ALU_G___MOV_G(opcode_grouping_unit_1_alu_g___mov_g), .CALL___LOAD(opcode_grouping_unit_1_call___load),
    .STORE_G___POP(opcode_grouping_unit_1_store_g___pop), .RET___POP(opcode_grouping_unit_1_ret___pop),
    .IMMD_T1(opcode_grouping_unit_1_immd_t1), .MAR_T2(opcode_grouping_unit_1_mar_t2),
    .MDR_T2(opcode_grouping_unit_1_mdr_t2), .RESERVE___HALT(opcode_grouping_unit_1_reserve___halt),
    .NOP(opcode_grouping_unit_1_nop));  // open: LOAD___PUSH
  or or_1 (or_1_out, state_machine_1_t3, state_machine_1_t5);
  and and_1 (and_1_out, opcode_decode_unit_1_pop, state_machine_1_t2);
  and and_2 (and_2_out, opcode_decode_unit_1_load, state_machine_1_t3);
  or or_2 (or_2_out, state_machine_1_t2, state_machine_1_t5);
  and and_3 (and_3_out, opcode_decode_unit_1_call, or_1_out);
  or or_3 (or_3_out, and_1_out, and_2_out);
  and and_4 (and_4_out, opcode_decode_unit_1_ret, or_2_out);
  or or_4 (or_4_out, opcode_grouping_unit_1_cmp___alu_g, opcode_decode_unit_1_mov_group);
  and and_5 (and_5_out, opcode_grouping_unit_1_jmp___branch_g, state_machine_1_t2);
  or or_5 (or_5_out, opcode_grouping_unit_1_store_g___pop, opcode_decode_unit_1_push);
  and and_6 (and_6_out, opcode_grouping_unit_1_call___ret, state_machine_1_t7);
  and and_7 (and_7_out, opcode_decode_unit_1_load, state_machine_1_t4);
  and and_8 (SIGNALS_TOP[11], opcode_grouping_unit_1_reserve___halt, state_machine_1_t1);
  and and_9 (and_9_out, opcode_decode_unit_1_jmp, state_machine_1_t2);
  and and_10 (and_10_out, opcode_decode_unit_1_branch_taken, state_machine_1_t2);
  and and_11 (and_11_out, opcode_grouping_unit_1_immd_t1, state_machine_1_t1);
  and and_12 (and_12_out, opcode_grouping_unit_1_call___ret, state_machine_1_t7);
  and and_13 (and_13_out, opcode_grouping_unit_1_alu_g___mov_g, state_machine_1_t1);
  and and_14 (and_14_out, opcode_decode_unit_1_pop, state_machine_1_t3);
  and and_15 (and_15_out, opcode_decode_unit_1_load, state_machine_1_t4);
  and and_16 (SIGNALS_TOP[0], state_machine_1_t1, opcode_grouping_unit_1_cmp___alu_g);
  and and_17 (SIGNALS_BOTTOM[7], state_machine_1_t1, opcode_grouping_unit_1_immd_t1);
  or or_6 (or_6_out, state_machine_1_t2, state_machine_1_t4);
  or or_7 (or_7_out, state_machine_1_t3, state_machine_1_t6);
  and and_18 (and_18_out, state_machine_1_t1, opcode_decode_unit_1_push);
  and and_19 (and_19_out, opcode_decode_unit_1_pop, state_machine_1_t2);
  and and_20 (and_20_out, opcode_grouping_unit_1_ret___pop, state_machine_1_t1);
  and and_21 (and_21_out, opcode_grouping_unit_1_mar_t2, state_machine_1_t2);
  or or_8 (or_8_out, state_machine_1_t3, state_machine_1_t5);
  and and_22 (and_22_out, opcode_decode_unit_1_ret, state_machine_1_t4);
  and and_23 (and_23_out, opcode_decode_unit_1_push, state_machine_1_t1);
  and and_24 (and_24_out, opcode_grouping_unit_1_mdr_t2, state_machine_1_t2);
  and and_25 (and_25_out, opcode_grouping_unit_1_call___load, state_machine_1_t3);
  and and_26 (and_26_out, opcode_grouping_unit_1_call___ret, state_machine_1_t5);
  and and_27 (and_27_out, opcode_decode_unit_1_call, state_machine_1_t2);
  and and_28 (and_28_out, opcode_decode_unit_1_ret, state_machine_1_t6);
  and and_29 (and_29_out, state_machine_1_t2, opcode_decode_unit_1_call);
  and and_30 (and_30_out, opcode_decode_unit_1_ret, state_machine_1_t3);
  or or_9 (or_9_out, state_machine_1_t2, state_machine_1_t4);
  and and_31 (and_31_out, opcode_decode_unit_1_push, state_machine_1_t1);
  or or_10 (or_10_out, state_machine_1_t3, state_machine_1_t6);
  and and_32 (SIGNALS_BOTTOM[3], opcode_decode_unit_1_call, state_machine_1_t5);
  and and_33 (and_33_out, opcode_grouping_unit_1_jmp___branch_g, state_machine_1_t2);
  and and_34 (and_34_out, state_machine_1_t7, opcode_decode_unit_1_call);
  and and_35 (SIGNALS_BOTTOM[11], opcode_decode_unit_1_ret, state_machine_1_t7);
  and and_36 (and_36_out, state_machine_1_t1, opcode_decode_unit_1_alu_group);
  and and_37 (and_37_out, state_machine_1_t3, opcode_decode_unit_1_pop);
  and and_38 (and_38_out, state_machine_1_t4, opcode_decode_unit_1_load);
  and and_39 (and_39_out, or_5_out, state_machine_1_t3);
  or or_11 (or_11_out, and_9_out, and_10_out);
  and and_40 (and_40_out, opcode_grouping_unit_1_ret___pop, state_machine_1_t1);
  or or_12 (or_12_out, state_machine_1_t3, state_machine_1_t5);
  and and_41 (and_41_out, opcode_decode_unit_1_ret, state_machine_1_t4);
  and and_42 (and_42_out, opcode_decode_unit_1_push, state_machine_1_t2);
  or or_13 (or_13_out, or_3_out, and_4_out);
  and and_43 (and_43_out, opcode_decode_unit_1_store, state_machine_1_t2);
  and and_44 (and_44_out, opcode_decode_unit_1_push, state_machine_1_t1);
  or or_14 (or_14_out, state_machine_1_t4, state_machine_1_t6);
  or or_15 (or_15_out, opcode_decode_unit_1_push, opcode_decode_unit_1_store_group);
  and and_45 (and_45_out, opcode_grouping_unit_1_ret___pop, state_machine_1_t2);
  and and_46 (and_46_out, opcode_decode_unit_1_load, state_machine_1_t3);
  and and_47 (and_47_out, opcode_decode_unit_1_ret, state_machine_1_t5);
  or or_16 (or_16_out, or_4_out, opcode_grouping_unit_1_nop);
  or or_17 (or_17_out, SIGNALS_BOTTOM[8], or_11_out);
  or or_18 (or_18_out, and_11_out, and_12_out);
  or or_19 (or_19_out, and_13_out, and_14_out);
  and and_48 (and_48_out, or_6_out, opcode_decode_unit_1_call);
  and and_49 (and_49_out, or_7_out, opcode_decode_unit_1_ret);
  or or_20 (or_20_out, and_18_out, and_19_out);
  or or_21 (or_21_out, and_20_out, and_21_out);
  and and_50 (and_50_out, or_8_out, opcode_decode_unit_1_call);
  or or_22 (or_22_out, and_23_out, and_24_out);
  or or_23 (or_23_out, and_25_out, and_26_out);
  or or_24 (SIGNALS_BOTTOM[4], and_27_out, and_28_out);
  or or_25 (SIGNALS_BOTTOM[5], and_29_out, and_30_out);
  and and_51 (and_51_out, or_9_out, opcode_decode_unit_1_call);
  and and_52 (SIGNALS_BOTTOM[6], or_10_out, opcode_decode_unit_1_ret);
  or or_26 (SIGNALS_BOTTOM[10], and_33_out, and_34_out);
  or or_27 (or_27_out, opcode_decode_unit_1_alu_group, opcode_decode_unit_1_mov);
  or or_28 (or_28_out, and_37_out, and_38_out);
  or or_29 (or_29_out, and_41_out, and_42_out);
  or or_30 (or_30_out, and_43_out, and_44_out);
  or or_31 (or_31_out, and_45_out, and_46_out);
  and and_53 (and_53_out, or_16_out, state_machine_1_t1);
  or or_32 (or_32_out, and_5_out, and_39_out);
  or or_33 (or_33_out, and_6_out, and_7_out);
  or or_34 (SIGNALS_BOTTOM[9], or_17_out, or_18_out);
  or or_35 (SIGNALS_TOP[1], or_19_out, and_15_out);
  or or_36 (or_36_out, and_48_out, and_49_out);
  or or_37 (or_37_out, and_50_out, and_22_out);
  or or_38 (or_38_out, and_51_out, and_31_out);
  and and_54 (SIGNALS_TOP[2], or_27_out, state_machine_1_t1);
  and and_55 (and_55_out, opcode_decode_unit_1_call, or_12_out);
  and and_56 (and_56_out, opcode_decode_unit_1_call, or_14_out);
  and and_57 (and_57_out, state_machine_1_t3, or_15_out);
  or or_39 (SIGNALS_TOP[5], or_31_out, and_47_out);
  or or_40 (SIGNALS_TOP[6], or_22_out, or_23_out);
  or or_41 (SIGNALS_TOP[3], and_36_out, or_28_out);
  or or_42 (or_42_out, and_40_out, and_55_out);
  or or_43 (SIGNALS_TOP[9], and_3_out, or_13_out);
  or or_44 (SIGNALS_TOP[8], and_3_out, or_30_out);
  or or_45 (or_45_out, and_53_out, or_32_out);
  or or_46 (or_46_out, or_36_out, or_20_out);
  or or_47 (SIGNALS_TOP[7], or_21_out, or_37_out);
  or or_48 (SIGNALS_BOTTOM[1], SIGNALS_BOTTOM[2], or_38_out);
  or or_49 (SIGNALS_TOP[4], and_56_out, and_57_out);
  or or_50 (or_50_out, or_45_out, or_33_out);
  or or_51 (SIGNALS_TOP[10], or_42_out, or_29_out);
  or or_52 (SIGNALS_BOTTOM[0], SIGNALS_BOTTOM[2], or_46_out);

  // Notes on the sheet:
  //   HALT_WE
  //   FLAGS_WE
  //   IMMD_WE
  //   TEMP_L_WE
  //   TEMP_H_WE
  //   IR_WE
  //   PC_WE
  //   REG_WE
  //   MDR_WE
  //   TEMP_LH_SEL
  //   PC_MUX[L]
  //   PC_MUX[H]
  //   REG_MUX[L]
  //   REG_MUX[H]
  //   MDR_MUX[0]
  //   SP_MUX[0]
  //   TEMP_MUX
  //   MEM_WR
  //   MEM_RD
  //   STATE_RESET_WE
  //   MAR_WE
  //   SP_MUX[1]
  //   MAR_MUX
  //   MDR_MUX[1]
  //   SP_WE
  //   BY - @VENUDAYYAM
endmodule

module IO_SELECT (
  input  MAR_WE,
  input  MDR_WE,
  input  MEM_RD,
  input  MEM_WR,
  input  [15:0] FROM_IMMD,
  output MAR_WE_2,
  output MDR_WE_2,
  output MEM_RD_2,
  output MEM_WR_2,
  output IO_SEL
);

  wire and_1_out, and_2_out, not_1_out;

  and and_1 (and_1_out, FROM_IMMD[12], FROM_IMMD[13]);
  and and_2 (and_2_out, FROM_IMMD[14], FROM_IMMD[15]);
  and and_3 (IO_SEL, and_1_out, and_2_out);
  not not_1 (not_1_out, IO_SEL);
  and and_4 (MAR_WE_2, MAR_WE, not_1_out);
  and and_5 (MDR_WE_2, MDR_WE, not_1_out);
  and and_6 (MEM_RD_2, MEM_RD, not_1_out);
  and and_7 (MEM_WR_2, MEM_WR, not_1_out);
endmodule

module IO_READ (
  input  WE,
  input  CLK,
  input  RESET,
  input  [15:0] FROM_IMMD,
  input  [7:0] KEY_DATA_IN,
  input  KEY_AVAIL,
  output B0,
  output B1,
  output [7:0] IO_DATA_OUT
);

  wire [7:0] KEY_VALUE_PRESSED_dout, undriven, undriven_2;

  _8BIT_REGISTER KEY_VALUE_PRESSED (
    .DIN(KEY_DATA_IN), .WE(WE), .CLK(CLK), .RESET(RESET), .DOUT(KEY_VALUE_PRESSED_dout));
  _8BIT_4_TO_1_MUX u_8bit_4_to_1_mux_1 (
    .DIN(KEY_VALUE_PRESSED_dout), .DIN_2({{7{1'b0}}, KEY_AVAIL}), .DIN_3(undriven), .DIN_4(undriven_2),
    .S0(FROM_IMMD[0]), .S1(FROM_IMMD[1]), .ALU_OUT(IO_DATA_OUT));

  assign B0 = FROM_IMMD[0];
  assign B1 = FROM_IMMD[1];
endmodule

module IO_UNIT (
  input  CLK,
  input  RESET,
  input  MAR_WE,
  input  MDR_WE,
  input  MEM_RD,
  input  MEM_WR,
  input  [15:0] FROM_IMMD,
  input  [7:0] KEY_DATA,
  input  KEY_AVAIL,
  output MAR_WE_2,
  output MDR_WE_2,
  output MEM_RD_2,
  output MEM_WR_2,
  output IO_SEL,
  output DISPLAY_ENABLE,
  output KEYBOARD_ENABLE,
  output [7:0] IO_DATA_OUT
);

  wire and_1_out, and_2_out, and_3_out, and_4_out, io_read_1_b0, io_read_1_b1, not_1_out, not_2_out;

  IO_SELECT io_select_1 (
    .MAR_WE(MAR_WE), .MDR_WE(MDR_WE), .MEM_RD(MEM_RD), .MEM_WR(MEM_WR), .FROM_IMMD(FROM_IMMD),
    .MAR_WE_2(MAR_WE_2), .MDR_WE_2(MDR_WE_2), .MEM_RD_2(MEM_RD_2), .MEM_WR_2(MEM_WR_2), .IO_SEL(IO_SEL));
  IO_READ io_read_1 (
    .FROM_IMMD(FROM_IMMD), .KEY_DATA_IN(KEY_DATA), .KEY_AVAIL(KEY_AVAIL), .WE(KEYBOARD_ENABLE), .CLK(CLK),
    .RESET(RESET), .B0(io_read_1_b0), .B1(io_read_1_b1), .IO_DATA_OUT(IO_DATA_OUT));
  and and_1 (and_1_out, IO_SEL, MEM_RD);
  and and_2 (and_2_out, IO_SEL, MEM_WR);
  not not_1 (not_1_out, io_read_1_b0);
  not not_2 (not_2_out, io_read_1_b1);
  and and_3 (and_3_out, io_read_1_b1, not_1_out);
  and and_4 (and_4_out, not_1_out, not_2_out);
  and and_5 (DISPLAY_ENABLE, and_2_out, and_3_out);
  and and_6 (KEYBOARD_ENABLE, and_1_out, and_4_out);
endmodule

// CPU_00
module CPU_WITHOUT_IO (
  input  RESET,
  output [7:0] CURRENT_STATE,
  output [15:0] PC_VALUE,
  output [4:0] OPCODE
);

  wire and_1_out, CLOCK_out, d_flip_flop_with_write_enable_1_q, not_1_out;
  wire [1:0] control_unit_1_signals_bottom, control_unit_1_signals_bottom_3, control_unit_1_signals_top_2,
       fetch_unit_1_ir_out;
  wire [2:0] fetch_unit_1_ir_out_2, fetch_unit_1_ir_out_3, fetch_unit_1_ir_out_4;
  wire [7:0] alu_1_alu_out, alu_1_flags, data_memory_unit_1_mdr_out, flag_register_1_out,
       n8_register_file_1_read_a, n8_register_file_1_read_b, temporary_register_unit_1_to_mdr_mux;
  wire [9:0] control_unit_1_signals_bottom_2;
  wire [11:0] control_unit_1_signals_top;
  wire [15:0] fetch_unit_1_immd_out, stack_pointer_unit_1_stack_out, temporary_register_unit_1_to_pc;

  D_FLIP_FLOP_WITH_WRITE_ENABLE d_flip_flop_with_write_enable_1 (
    .D(1'b1), .WE(control_unit_1_signals_top[11]), .CLOCK(CLOCK_out), .RESET(RESET),
    .Q(d_flip_flop_with_write_enable_1_q));
  Clock CLOCK (.out(CLOCK_out));
  not not_1 (not_1_out, d_flip_flop_with_write_enable_1_q);
  FETCH_UNIT fetch_unit_1 (
    .TEMP_REG(temporary_register_unit_1_to_pc), .PC_MUX(control_unit_1_signals_bottom_3),
    .PC_WE(control_unit_1_signals_bottom_2[9]), .CLK(and_1_out), .RESET(RESET),
    .IR_WE(control_unit_1_signals_bottom_2[8]), .IMMD_REG_WE(control_unit_1_signals_bottom_2[7]),
    .IR_OUT({OPCODE, fetch_unit_1_ir_out_2, fetch_unit_1_ir_out_4, fetch_unit_1_ir_out_3, fetch_unit_1_ir_out}),
    .IMMD_OUT(fetch_unit_1_immd_out), .PC(PC_VALUE));
  and and_1 (and_1_out, CLOCK_out, not_1_out);
  CONTROL_UNIT control_unit_1 (
    .FROM_IR({OPCODE, fetch_unit_1_ir_out_2, fetch_unit_1_ir_out_4, fetch_unit_1_ir_out_3, fetch_unit_1_ir_out}),
    .FROM_FR(flag_register_1_out), .CLK(and_1_out), .RESET(RESET), .CURR_STATE(CURRENT_STATE),
    .SIGNALS_TOP({control_unit_1_signals_top[11:4], control_unit_1_signals_top_2, control_unit_1_signals_top[1:0]}),
    .SIGNALS_BOTTOM({control_unit_1_signals_bottom_3, control_unit_1_signals_bottom_2[9:3], control_unit_1_signals_bottom, control_unit_1_signals_bottom_2[0]}));  // open: NEXT_STATE
  TEMPORARY_REGISTER_UNIT temporary_register_unit_1 (
    .FROM_PC(PC_VALUE), .FROM_MDR(data_memory_unit_1_mdr_out), .TEMP_SRC(control_unit_1_signals_bottom_2[6]),
    .TEMP_H_WE(control_unit_1_signals_bottom_2[5]), .TEMP_L_WE(control_unit_1_signals_bottom_2[4]),
    .CLK(and_1_out), .RESET(RESET), .TEMP_LH_SEL(control_unit_1_signals_bottom_2[3]),
    .TO_PC(temporary_register_unit_1_to_pc), .TO_MDR_MUX(temporary_register_unit_1_to_mdr_mux));
  STACK_POINTER_UNIT stack_pointer_unit_1 (
    .SP_SEL(control_unit_1_signals_bottom), .SP_WE(control_unit_1_signals_bottom_2[0]), .CLK(and_1_out),
    .RESET(RESET), .STACK_OUT(stack_pointer_unit_1_stack_out));
  DATA_MEMORY_UNIT data_memory_unit_1 (
    .IMM_DATA({fetch_unit_1_ir_out_4, fetch_unit_1_ir_out_3, fetch_unit_1_ir_out}),
    .REG_A(n8_register_file_1_read_a), .TEMP_REG_LH(temporary_register_unit_1_to_mdr_mux),
    .IMMD_OUT(fetch_unit_1_immd_out), .SP_OUT(stack_pointer_unit_1_stack_out),
    .MAR_MUX(control_unit_1_signals_top[10]), .MDR_MUX(control_unit_1_signals_top[9:8]),
    .MAR_WE(control_unit_1_signals_top[7]), .MDR_WE(control_unit_1_signals_top[6]),
    .MEM_RD(control_unit_1_signals_top[5]), .MEM_WR(control_unit_1_signals_top[4]), .CLK(and_1_out),
    .RESET(RESET), .MDR_OUT(data_memory_unit_1_mdr_out));
  _8_REGISTER_FILE u_8_register_file_1 (
    .IMM_DATA({fetch_unit_1_ir_out_4, fetch_unit_1_ir_out_3, fetch_unit_1_ir_out}),
    .MDR_OUT(data_memory_unit_1_mdr_out), .ALU_OUT(alu_1_alu_out), .REG_MUX(control_unit_1_signals_top_2),
    .WRITE_SELECT(fetch_unit_1_ir_out_2), .REG_WE(control_unit_1_signals_top[1]), .CLK(and_1_out),
    .RESET(RESET), .A_SELECT(fetch_unit_1_ir_out_4), .B_SELECT(fetch_unit_1_ir_out_3),
    .READ_A(n8_register_file_1_read_a), .READ_B(n8_register_file_1_read_b));
  ALU alu_1 (
    .A0_07(n8_register_file_1_read_a), .B0_B7(n8_register_file_1_read_b), .OPCODE(OPCODE),
    .ALU_OUT(alu_1_alu_out), .FLAGS(alu_1_flags));
  FLAG_REGISTER flag_register_1 (
    .IN(alu_1_flags), .FLAG_WE(control_unit_1_signals_top[0]), .CLK(and_1_out), .RESET(RESET),
    .OUT(flag_register_1_out));
endmodule
