// Logisim project REGISTERS.circ as structural Verilog: 14 circuits, main circuit RS_LATCH_WITH_RESET
// RS_LATCH
module RS_LATCH_WITH_RESET (
  input  RESET,
  input  R,
  input  S,
  output Q,
  output Q_prime
);

  wire n1bit_2_to_1_mux_1_dout, n1bit_2_to_1_mux_2_dout;

  _1BIT_2_TO_1_MUX u_1bit_2_to_1_mux_1 (.DATA(R), .DATA_2(1'b1), .SELECT(RESET), .DOUT(n1bit_2_to_1_mux_1_dout));
  _1BIT_2_TO_1_MUX u_1bit_2_to_1_mux_2 (.DATA(S), .DATA_2(1'b0), .SELECT(RESET), .DOUT(n1bit_2_to_1_mux_2_dout));
  nor nor_1 (Q, n1bit_2_to_1_mux_1_dout, Q_prime);
  nor nor_2 (Q_prime, Q, n1bit_2_to_1_mux_2_dout);
endmodule

// RS_LATCH
module GATED_RS_LATCH (
  input  ENABLE,
  input  RESET,
  input  R,
  input  S,
  output Q
);

  wire and_1_out, and_2_out;

  and and_1 (and_1_out, ENABLE, R);
  and and_2 (and_2_out, ENABLE, S);
  RS_LATCH_WITH_RESET rs_latch_with_reset_1 (.R(and_1_out), .S(and_2_out), .RESET(RESET), .Q(Q));  // open: Q_prime
endmodule

module D_LATCH (
  input  ENABLE,
  input  RESET,
  input  D,
  output Q
);

  wire not_1_out;

  not not_1 (not_1_out, D);
  GATED_RS_LATCH gated_rs_latch_1 (.R(not_1_out), .S(D), .ENABLE(ENABLE), .RESET(RESET), .Q(Q));
endmodule

// DFF
module D_FLIP_FLOP_MASTER_SLAVE (
  input  CLOCK,
  input  RESET,
  input  D,
  output Q
);

  wire d_latch_1_q, not_1_out;

  not not_1 (not_1_out, CLOCK);
  D_LATCH d_latch_1 (.D(D), .ENABLE(not_1_out), .RESET(RESET), .Q(d_latch_1_q));
  D_LATCH d_latch_2 (.D(d_latch_1_q), .ENABLE(CLOCK), .RESET(RESET), .Q(Q));
endmodule

// DFF-WE
module D_FLIP_FLOP_WITH_WRITE_ENABLE (
  input  WE,
  input  CLOCK,
  input  RESET,
  input  D,
  output Q
);

  wire n1bit_2_to_1_mux_1_dout;

  _1BIT_2_TO_1_MUX u_1bit_2_to_1_mux_1 (.DATA(Q), .DATA_2(D), .SELECT(WE), .DOUT(n1bit_2_to_1_mux_1_dout));
  D_FLIP_FLOP_MASTER_SLAVE d_flip_flop_master_slave_1 (
    .D(n1bit_2_to_1_mux_1_dout), .CLOCK(CLOCK), .RESET(RESET), .Q(Q));
endmodule

// REG4
module _4BIT_REGISTER (
  input  WE,
  input  CLK,
  input  RESET,
  input  [3:0] D0_D3,
  output [3:0] D0_D3_2
);

  D_FLIP_FLOP_WITH_WRITE_ENABLE d_flip_flop_with_write_enable_1 (
    .D(D0_D3[0]), .WE(WE), .CLOCK(CLK), .RESET(RESET), .Q(D0_D3_2[0]));
  D_FLIP_FLOP_WITH_WRITE_ENABLE d_flip_flop_with_write_enable_2 (
    .D(D0_D3[1]), .WE(WE), .CLOCK(CLK), .RESET(RESET), .Q(D0_D3_2[1]));
  D_FLIP_FLOP_WITH_WRITE_ENABLE d_flip_flop_with_write_enable_3 (
    .D(D0_D3[2]), .WE(WE), .CLOCK(CLK), .RESET(RESET), .Q(D0_D3_2[2]));
  D_FLIP_FLOP_WITH_WRITE_ENABLE d_flip_flop_with_write_enable_4 (
    .D(D0_D3[3]), .WE(WE), .CLOCK(CLK), .RESET(RESET), .Q(D0_D3_2[3]));
endmodule

// REG8
module _8BIT_REGISTER (
  input  WE,
  input  CLK,
  input  RESET,
  input  [7:0] DIN,
  output [7:0] DOUT
);

  _4BIT_REGISTER u_4bit_register_1 (.D0_D3(DIN[3:0]), .WE(WE), .CLK(CLK), .RESET(RESET), .D0_D3_2(DOUT[3:0]));
  _4BIT_REGISTER u_4bit_register_2 (.D0_D3(DIN[7:4]), .WE(WE), .CLK(CLK), .RESET(RESET), .D0_D3_2(DOUT[7:4]));
endmodule

// REG16
module _16BIT_REGISTER (
  input  WE,
  input  CLK,
  input  RESET,
  input  [15:0] DIN,
  output [15:0] DOUT
);

  _8BIT_REGISTER u_8bit_register_1 (.DIN(DIN[7:0]), .WE(WE), .CLK(CLK), .RESET(RESET), .DOUT(DOUT[7:0]));
  _8BIT_REGISTER u_8bit_register_2 (.DIN(DIN[15:8]), .WE(WE), .CLK(CLK), .RESET(RESET), .DOUT(DOUT[15:8]));
endmodule

// 8_REG_FILE
module _8_REGISTER_FILE (
  input  [1:0] REG_MUX,
  input  [2:0] WRITE_SELECT,
  input  REG_WE,
  input  CLK,
  input  RESET,
  input  [2:0] A_SELECT,
  input  [2:0] B_SELECT,
  input  [7:0] IMM_DATA,
  input  [7:0] MDR_OUT,
  input  [7:0] ALU_OUT,
  output [7:0] READ_A,
  output [7:0] READ_B
);

  wire [7:0] n3_to_8_decoder_with_enable_1_out, n8bit_4_to_1_mux_1_alu_out, n8bit_register_1_dout,
       n8bit_register_2_dout, n8bit_register_3_dout, n8bit_register_4_dout, n8bit_register_5_dout,
       n8bit_register_6_dout, n8bit_register_7_dout, n8bit_register_8_dout;

  _8BIT_4_TO_1_MUX u_8bit_4_to_1_mux_1 (
    .DIN(IMM_DATA), .DIN_2(READ_A), .DIN_3(MDR_OUT), .DIN_4(ALU_OUT), .S0(REG_MUX[0]), .S1(REG_MUX[1]),
    .ALU_OUT(n8bit_4_to_1_mux_1_alu_out));
  _3_TO_8_DECODER_WITH_ENABLE u_3_to_8_decoder_with_enable_1 (
    .S2(WRITE_SELECT[2]), .S1(WRITE_SELECT[1]), .S0(WRITE_SELECT[0]), .ENABLE(REG_WE),
    .OUT(n3_to_8_decoder_with_enable_1_out));
  _8BIT_REGISTER u_8bit_register_1 (
    .DIN(n8bit_4_to_1_mux_1_alu_out), .WE(n3_to_8_decoder_with_enable_1_out[0]), .CLK(CLK), .RESET(RESET),
    .DOUT(n8bit_register_1_dout));
  _8BIT_REGISTER u_8bit_register_2 (
    .DIN(n8bit_4_to_1_mux_1_alu_out), .WE(n3_to_8_decoder_with_enable_1_out[1]), .CLK(CLK), .RESET(RESET),
    .DOUT(n8bit_register_2_dout));
  _8BIT_REGISTER u_8bit_register_3 (
    .DIN(n8bit_4_to_1_mux_1_alu_out), .WE(n3_to_8_decoder_with_enable_1_out[2]), .CLK(CLK), .RESET(RESET),
    .DOUT(n8bit_register_3_dout));
  _8BIT_REGISTER u_8bit_register_4 (
    .DIN(n8bit_4_to_1_mux_1_alu_out), .WE(n3_to_8_decoder_with_enable_1_out[3]), .CLK(CLK), .RESET(RESET),
    .DOUT(n8bit_register_4_dout));
  _8BIT_REGISTER u_8bit_register_5 (
    .DIN(n8bit_4_to_1_mux_1_alu_out), .WE(n3_to_8_decoder_with_enable_1_out[4]), .CLK(CLK), .RESET(RESET),
    .DOUT(n8bit_register_5_dout));
  _8BIT_REGISTER u_8bit_register_6 (
    .DIN(n8bit_4_to_1_mux_1_alu_out), .WE(n3_to_8_decoder_with_enable_1_out[5]), .CLK(CLK), .RESET(RESET),
    .DOUT(n8bit_register_6_dout));
  _8BIT_REGISTER u_8bit_register_7 (
    .DIN(n8bit_4_to_1_mux_1_alu_out), .WE(n3_to_8_decoder_with_enable_1_out[6]), .CLK(CLK), .RESET(RESET),
    .DOUT(n8bit_register_7_dout));
  _8BIT_REGISTER u_8bit_register_8 (
    .DIN(n8bit_4_to_1_mux_1_alu_out), .WE(n3_to_8_decoder_with_enable_1_out[7]), .CLK(CLK), .RESET(RESET),
    .DOUT(n8bit_register_8_dout));
  _8BIT_8_TO_1_MUX u_8bit_8_to_1_mux_1 (
    .DIN(n8bit_register_1_dout), .DIN_2(n8bit_register_2_dout), .DIN_3(n8bit_register_3_dout),
    .DIN_4(n8bit_register_4_dout), .DIN_5(n8bit_register_5_dout), .DIN_6(n8bit_register_6_dout),
    .DIN_7(n8bit_register_7_dout), .DIN_8(n8bit_register_8_dout), .S0(A_SELECT[0]), .S1(A_SELECT[1]),
    .S2(A_SELECT[2]), .ALU_OUT(READ_A));
  _8BIT_8_TO_1_MUX u_8bit_8_to_1_mux_2 (
    .DIN(n8bit_register_1_dout), .DIN_2(n8bit_register_2_dout), .DIN_3(n8bit_register_3_dout),
    .DIN_4(n8bit_register_4_dout), .DIN_5(n8bit_register_5_dout), .DIN_6(n8bit_register_6_dout),
    .DIN_7(n8bit_register_7_dout), .DIN_8(n8bit_register_8_dout), .S0(B_SELECT[0]), .S1(B_SELECT[1]),
    .S2(B_SELECT[2]), .ALU_OUT(READ_B));
endmodule

// DECODER
module _2_TO_4_DECODER (
  input  A,
  input  B,
  output O1,
  output O2,
  output O3,
  output O4
);

  wire not_1_out, not_2_out;

  not not_1 (not_1_out, A);
  not not_2 (not_2_out, B);
  and and_1 (O1, not_1_out, not_2_out);
  and and_2 (O2, not_1_out, B);
  and and_3 (O3, A, not_2_out);
  and and_4 (O4, A, B);
endmodule

// DECODER
module _3_TO_8_DECODER (
  input  S2,
  input  S1,
  input  S0,
  output [7:0] OUT
);

  wire not_1_out;

  not not_1 (not_1_out, S2);
  _2_TO_4_DECODE_WITH_ENABLE u_2_to_4_decode_with_enable_1 (
    .A(S1), .B(S0), .ENABLE(not_1_out), .O1(OUT[0]), .O2(OUT[1]), .O3(OUT[2]), .O4(OUT[3]));
  _2_TO_4_DECODE_WITH_ENABLE u_2_to_4_decode_with_enable_2 (
    .A(S1), .B(S0), .ENABLE(S2), .O1(OUT[4]), .O2(OUT[5]), .O3(OUT[6]), .O4(OUT[7]));
endmodule

// DECODER
module _2_TO_4_DECODE_WITH_ENABLE (
  input  A,
  input  B,
  input  ENABLE,
  output O1,
  output O2,
  output O3,
  output O4
);

  wire and_1_out, and_2_out, and_3_out, and_4_out, not_1_out, not_2_out;

  not not_1 (not_1_out, A);
  not not_2 (not_2_out, B);
  and and_1 (and_1_out, not_1_out, not_2_out);
  and and_2 (and_2_out, not_1_out, B);
  and and_3 (and_3_out, A, not_2_out);
  and and_4 (and_4_out, A, B);
  and and_5 (O1, ENABLE, and_1_out);
  and and_6 (O2, ENABLE, and_2_out);
  and and_7 (O3, ENABLE, and_3_out);
  and and_8 (O4, ENABLE, and_4_out);
endmodule

// DECODER
module _3_TO_8_DECODER_WITH_ENABLE (
  input  S2,
  input  S1,
  input  S0,
  input  ENABLE,
  output [7:0] OUT
);

  wire not_1_out;
  wire [7:0] n2_to_4_decode_with_enable_1_o1;

  not not_1 (not_1_out, S2);
  _2_TO_4_DECODE_WITH_ENABLE u_2_to_4_decode_with_enable_1 (
    .A(S1), .B(S0), .ENABLE(not_1_out), .O1(n2_to_4_decode_with_enable_1_o1[0]),
    .O2(n2_to_4_decode_with_enable_1_o1[1]), .O3(n2_to_4_decode_with_enable_1_o1[2]),
    .O4(n2_to_4_decode_with_enable_1_o1[3]));
  _2_TO_4_DECODE_WITH_ENABLE u_2_to_4_decode_with_enable_2 (
    .A(S1), .B(S0), .ENABLE(S2), .O1(n2_to_4_decode_with_enable_1_o1[4]),
    .O2(n2_to_4_decode_with_enable_1_o1[5]), .O3(n2_to_4_decode_with_enable_1_o1[6]),
    .O4(n2_to_4_decode_with_enable_1_o1[7]));
  _8BIT_AND u_8bit_and_1 (.A({8{ENABLE}}), .B(n2_to_4_decode_with_enable_1_o1), .A_AND_B(OUT));
endmodule

// DECODER
module _4_TO_16_DECODER (
  input  S3,
  input  S2,
  input  S1,
  input  S0,
  output [15:0] OUT
);

  wire not_1_out;

  not not_1 (not_1_out, S3);
  _3_TO_8_DECODER_WITH_ENABLE u_3_to_8_decoder_with_enable_1 (
    .S2(S2), .S1(S1), .S0(S0), .ENABLE(not_1_out), .OUT(OUT[7:0]));
  _3_TO_8_DECODER_WITH_ENABLE u_3_to_8_decoder_with_enable_2 (.S2(S2), .S1(S1), .S0(S0), .ENABLE(S3), .OUT(OUT[15:8]));
endmodule
